// Logisim project Logisim 01.circ as structural Verilog: 1 circuit, main circuit main
module main (
  input  in_1,
  input  in_2
);

  wire and_1_out, nor_1_out, not_1_out, not_2_out;

  not not_1 (not_1_out, in_2);
  not not_2 (not_2_out, in_1);
  nor nor_1 (nor_1_out, in_1, in_2);
  and and_1 (and_1_out, not_1_out, not_2_out);
  LED led_1 (.in(nor_1_out));
  LED led_2 (.in(and_1_out));
endmodule
