// Logisim project Logisim 05.circ as structural Verilog: 1 circuit, main circuit main
module main (
  input  in_1,
  input  in_2
);

  wire nor_1_out, xnor_1_out;

  xnor xnor_1 (xnor_1_out, in_1, in_2);
  nor nor_1 (nor_1_out, xnor_1_out, in_1);
  LED led_1 (.in(nor_1_out));
endmodule
