// Logisim project Logisim 07.circ as structural Verilog: 1 circuit, main circuit main
module main (
  input  in_1,
  input  in_2
);

  wire nor_1_out, nor_2_out, nor_3_out, nor_4_out, nor_5_out, not_1_out, xnor_1_out;

  not not_1 (not_1_out, in_2);
  xnor xnor_1 (xnor_1_out, in_1, not_1_out);
  nor nor_1 (nor_1_out, in_1, in_2);
  nor nor_2 (nor_2_out, nor_1_out, in_1);
  nor nor_3 (nor_3_out, nor_1_out, in_2);
  LED led_1 (.in(xnor_1_out));
  nor nor_4 (nor_4_out, nor_2_out, nor_3_out);
  nor nor_5 (nor_5_out, nor_1_out, nor_4_out);
  LED led_2 (.in(nor_5_out));
endmodule
