// Logisim project Logisim 08.circ as structural Verilog: 1 circuit, main circuit main
module main (
  input  in_1,
  input  in_2
);

  wire nand_1_out, nand_2_out, nand_3_out, nand_4_out, nand_5_out, not_1_out;

  not not_1 (not_1_out, in_2);
  nand nand_1 (nand_1_out, in_1, in_2);
  nand nand_2 (nand_2_out, in_1, not_1_out);
  nand nand_3 (nand_3_out, nand_1_out, in_1);
  nand nand_4 (nand_4_out, nand_3_out, nand_1_out);
  LED led_1 (.in(nand_2_out));
  LED led_2 (.in(nand_5_out));
  nand nand_5 (nand_5_out, nand_1_out, nand_4_out);
endmodule
