// Logisim project ExercicioE.circ as structural Verilog: 1 circuit, main circuit main
module main (
  input  in_1,
  input  in_2,
  input  in_3,
  output out_4,
  output out_5
);

  wire not_1_out, not_2_out, not_3_out, not_4_out, not_5_out, not_6_out, not_7_out, not_8_out, not_9_out,
       not_10_out, not_11_out, not_12_out, or_1_out, or_2_out, or_3_out, or_4_out, or_5_out, or_6_out,
       or_7_out;

  not not_1 (not_1_out, in_2);
  or or_1 (or_1_out, in_3, not_1_out, not_2_out);
  not not_2 (not_2_out, in_1);
  or or_2 (or_2_out, in_3, not_3_out, in_1);
  not not_3 (not_3_out, in_2);
  not not_4 (not_4_out, in_3);
  not not_5 (not_5_out, in_2);
  or or_3 (or_3_out, not_4_out, not_5_out, not_6_out);
  not not_6 (not_6_out, in_1);
  or or_4 (or_4_out, in_3, in_2, not_7_out);
  not not_7 (not_7_out, in_1);
  or or_5 (or_5_out, in_3, not_8_out);
  not not_8 (not_8_out, in_1);
  not not_9 (not_9_out, in_2);
  or or_6 (or_6_out, in_3, not_9_out, in_1);
  not not_10 (not_10_out, in_3);
  or or_7 (or_7_out, not_10_out, not_11_out, not_12_out);
  not not_11 (not_11_out, in_2);
  not not_12 (not_12_out, in_1);
  and and_1 (out_4, or_1_out, or_2_out, or_3_out, or_4_out);
  and and_2 (out_5, or_5_out, or_6_out, or_7_out);
endmodule
