// Logisim project Exercicio01.circ as structural Verilog: 1 circuit, main circuit main
module main (
  input  in_1,
  input  in_2,
  input  in_3,
  output out_4,
  output out_5
);

  wire and_1_out, and_2_out, nand_1_out, nand_2_out;

  and and_1 (and_1_out, in_2, in_3);
  and and_2 (and_2_out, in_1, in_3);
  nand nand_1 (nand_1_out, in_2, in_3);
  nand nand_2 (nand_2_out, in_1, in_3);
  and and_3 (out_4, and_1_out, and_2_out);
  nand nand_3 (out_5, nand_1_out, nand_2_out);
endmodule
