// Logisim project Exercicio02.circ as structural Verilog: 1 circuit, main circuit main
module main (
  input  in_1,
  input  in_2,
  input  in_3,
  output out_4
);

  wire nor_1_out, nor_2_out, nor_3_out, nor_4_out, nor_5_out, or_1_out;

  nor nor_1 (nor_1_out, or_1_out, or_1_out);
  or or_1 (or_1_out, in_2, in_1);
  nor nor_2 (nor_2_out, in_2, in_1);
  nor nor_3 (nor_3_out, nor_2_out, nor_2_out);
  nor nor_4 (nor_4_out, nor_1_out, in_3);
  nor nor_5 (nor_5_out, in_3, nor_3_out);
  or or_2 (out_4, nor_4_out, nor_5_out);
endmodule
