// Logisim project Exercicio03.circ as structural Verilog: 1 circuit, main circuit main
module main (
  input  b,
  input  a,
  input  in_3,
  input  in_4,
  output out_5
);

  wire and_1_out, and_2_out, and_3_out, and_4_out, and_5_out, nand_1_out, nand_2_out, nand_3_out, nand_4_out,
       nand_5_out, nor_1_out, not_1_out, not_2_out, not_3_out, not_4_out, or_1_out;

  and and_1 (and_1_out, a, b);
  nand nand_1 (nand_1_out, a, b);
  or or_1 (or_1_out, a, b);
  nor nor_1 (nor_1_out, a, b);
  not not_1 (not_1_out, in_4);
  and and_2 (and_2_out, not_1_out, not_2_out, and_1_out);
  not not_2 (not_2_out, in_3);
  and and_3 (and_3_out, in_4, not_3_out, nand_1_out);
  not not_3 (not_3_out, in_3);
  not not_4 (not_4_out, in_4);
  and and_4 (and_4_out, not_4_out, in_3, or_1_out);
  and and_5 (and_5_out, in_4, in_3, nor_1_out);
  nand nand_2 (nand_2_out, and_2_out, and_2_out);
  nand nand_3 (nand_3_out, and_3_out, and_3_out);
  nand nand_4 (nand_4_out, and_4_out, and_4_out);
  nand nand_5 (nand_5_out, and_5_out, and_5_out);
  nand nand_6 (out_5, nand_2_out, nand_3_out, nand_4_out, nand_5_out);
endmodule
