// Logisim project Exercicio04.circ as structural Verilog: 1 circuit, main circuit main
module main (
  input  B,
  input  A,
  input  E1,
  input  E0,
  output out_5
);

  wire and_1_out, and_2_out, and_3_out, and_4_out, nor_out, not_1_out, not_2_out, not_3_out, not_4_out,
       or_out, xnor_out, xor_out;

  or \or  (or_out, A, B);
  nor \nor  (nor_out, A, B);
  xor \xor  (xor_out, A, B);
  xnor \xnor  (xnor_out, A, B);
  not not_1 (not_1_out, E0);
  not not_2 (not_2_out, E1);
  and and_1 (and_1_out, not_1_out, not_2_out, or_out);
  not not_3 (not_3_out, E1);
  and and_2 (and_2_out, E0, not_3_out, nor_out);
  not not_4 (not_4_out, E0);
  and and_3 (and_3_out, not_4_out, E1, xor_out);
  and and_4 (and_4_out, E0, E1, xnor_out);
  or or_2 (out_5, and_1_out, and_2_out, and_3_out, and_4_out);
endmodule
