// Logisim project Exercicio06.circ as structural Verilog: 1 circuit, main circuit main
module main (
  input  in_1,
  input  in_2,
  input  in_3,
  input  in_4
);

  wire xnor_1_out, xnor_2_out, xnor_3_out, xor_1_out, xor_2_out, xor_3_out;

  xor xor_1 (xor_1_out, in_4, in_2);
  xor xor_2 (xor_2_out, in_3, in_1);
  xnor xnor_1 (xnor_1_out, in_4, in_2);
  xnor xnor_2 (xnor_2_out, in_3, in_1);
  xnor xnor_3 (xnor_3_out, xor_1_out, xor_2_out);
  ExactlyOne xor_3 (.out(xor_3_out), .in0(xnor_1_out), .in1(xnor_3_out), .in2(xnor_2_out));
endmodule
