// Logisim project Exercicio02.circ as structural Verilog: 1 circuit, main circuit main
module main (
  input  in_1,
  input  in_2,
  input  in_3,
  input  in_4,
  input  in_5,
  input  in_6,
  input  in_7,
  input  in_8,
  input  in_9,
  input  in_10,
  input  in_11,
  output out_12,
  output out_13,
  output out_14,
  output out_15,
  output out_16,
  output out_17
);

  wire and_1_out, and_2_out, and_3_out, and_4_out, and_5_out, and_6_out, and_7_out, and_8_out, and_9_out,
       and_10_out, not_1_out, not_2_out, not_3_out, not_4_out, not_5_out, not_6_out, not_7_out, not_8_out,
       not_9_out, not_10_out, or_1_out, or_2_out, or_3_out, or_4_out, xor_1_out, xor_2_out, xor_3_out,
       xor_5_out, xor_7_out;

  not not_1 (not_1_out, in_10);
  not not_2 (not_2_out, in_6);
  xor xor_1 (xor_1_out, in_7, in_2);
  and and_1 (and_1_out, in_2, not_3_out);
  not not_3 (not_3_out, in_7);
  xor xor_2 (xor_2_out, in_8, in_3);
  and and_2 (and_2_out, in_3, not_4_out);
  not not_4 (not_4_out, in_8);
  not not_5 (not_5_out, xor_3_out);
  xor xor_3 (xor_3_out, in_9, in_4);
  and and_3 (and_3_out, in_4, not_6_out);
  not not_6 (not_6_out, in_9);
  xor xor_4 (out_17, in_11, xor_5_out);
  and and_4 (and_4_out, in_11, not_7_out);
  not not_7 (not_7_out, xor_5_out);
  xor xor_5 (xor_5_out, in_10, in_5);
  or or_1 (or_1_out, and_4_out, and_5_out);
  and and_5 (and_5_out, in_5, not_1_out);
  xor xor_6 (out_13, or_2_out, xor_7_out);
  and and_6 (and_6_out, or_2_out, not_8_out);
  not not_8 (not_8_out, xor_7_out);
  xor xor_7 (xor_7_out, in_6, in_1);
  and and_7 (and_7_out, in_1, not_2_out);
  xor xor_8 (out_14, or_3_out, xor_1_out);
  and and_8 (and_8_out, or_3_out, not_9_out);
  not not_9 (not_9_out, xor_1_out);
  or or_2 (or_2_out, and_8_out, and_1_out);
  xor xor_9 (out_15, or_4_out, xor_2_out);
  and and_9 (and_9_out, or_4_out, not_10_out);
  not not_10 (not_10_out, xor_2_out);
  or or_3 (or_3_out, and_9_out, and_2_out);
  xor xor_10 (out_16, or_1_out, xor_3_out);
  and and_10 (and_10_out, or_1_out, not_5_out);
  or or_4 (or_4_out, and_10_out, and_3_out);
  or or_5 (out_12, and_6_out, and_7_out);
endmodule
