// Logisim project Exercicio01.circ as structural Verilog: 1 circuit, main circuit main
module main (
  input  in_1,
  input  in_2,
  input  in_3,
  input  in_4,
  input  in_5,
  input  in_6,
  input  in_7,
  input  in_8,
  input  in_9,
  input  in_10,
  input  in_11,
  output vai,
  output out_13,
  output out_14,
  output out_15,
  output out_16,
  output out_17,
  output out_18,
  output vai_2,
  output vai_3
);

  wire and_1_out, and_2_out, and_3_out, and_4_out, and_5_out, and_6_out, and_7_out, and_8_out, and_9_out,
       and_10_out, or_4_out, xor_1_out, xor_2_out, xor_3_out, xor_7_out, xor_8_out;

  and and_1 (and_1_out, in_10, in_5);
  xor xor_1 (xor_1_out, in_10, in_5);
  and and_2 (and_2_out, in_9, in_4);
  xor xor_2 (xor_2_out, in_9, in_4);
  and and_3 (and_3_out, in_8, in_3);
  xor xor_3 (xor_3_out, in_8, in_3);
  or or_1 (vai, and_1_out, and_4_out);
  and and_4 (and_4_out, xor_1_out, in_11);
  xor xor_4 (out_18, xor_1_out, in_11);
  or or_2 (vai_2, and_2_out, and_5_out);
  and and_5 (and_5_out, xor_2_out, vai);
  xor xor_5 (out_17, xor_2_out, vai);
  or or_3 (vai_3, and_3_out, and_6_out);
  and and_6 (and_6_out, xor_3_out, vai_2);
  xor xor_6 (out_16, xor_3_out, vai_2);
  and and_7 (and_7_out, in_7, in_2);
  xor xor_7 (xor_7_out, in_7, in_2);
  and and_8 (and_8_out, in_6, in_1);
  xor xor_8 (xor_8_out, in_6, in_1);
  or or_4 (or_4_out, and_7_out, and_9_out);
  and and_9 (and_9_out, xor_7_out, vai_3);
  xor xor_9 (out_15, xor_7_out, vai_3);
  and and_10 (and_10_out, or_4_out, xor_8_out);
  or or_5 (out_13, and_8_out, and_10_out);
  xor xor_10 (out_14, or_4_out, xor_8_out);
endmodule
