// Logisim project Exercicio04.circ as structural Verilog: 1 circuit, main circuit main
module main (
  input  in_1,
  input  in_2,
  input  in_3,
  input  in_4,
  input  in_5,
  input  in_6,
  input  in_7,
  input  in_8,
  input  in_9,
  input  in_10,
  output out_11,
  output out_12,
  output out_13,
  output out_14,
  output out_15,
  output out_16
);

  xor xor_1 (out_13, in_9, in_4);
  xor xor_2 (out_14, in_8, in_3);
  xor xor_3 (out_15, in_7, in_2);
  xor xor_4 (out_13, in_1, in_6);
  xor xor_5 (out_12, in_10, in_5);
  or or_1 (out_11, out_12, out_13, out_14, out_15, out_13);

  assign out_16 = out_13;
endmodule
