// Logisim project GUIA01.circ as structural Verilog: 2 circuits, main circuit main
module Projeto (
  input  in_1
);

  wire and_1_out, clock_1_out, d_ff_1_q, d_ff_2_q, d_ff_3_q, d_ff_4_q, d_ff_4_qn, not_1_out;

  Clock clock_1 (.out(clock_1_out));
  D_Flip_Flop d_ff_1 (.clk(clock_1_out), .D(in_1), .Q(d_ff_1_q));  // open: Qn, preset, en, reset
  D_Flip_Flop d_ff_2 (.clk(clock_1_out), .D(d_ff_1_q), .Q(d_ff_2_q));  // open: Qn, preset, en, reset
  D_Flip_Flop d_ff_3 (.clk(clock_1_out), .D(d_ff_2_q), .Q(d_ff_3_q));  // open: Qn, preset, en, reset
  D_Flip_Flop d_ff_4 (.clk(clock_1_out), .D(d_ff_3_q), .Q(d_ff_4_q), .Qn(d_ff_4_qn));  // open: preset, en, reset
  not not_1 (not_1_out, d_ff_2_q);
  and and_1 (and_1_out, d_ff_4_q, d_ff_3_q, not_1_out, d_ff_1_q);
endmodule

module main (
  input  in_1,
  output out_2
);

  wire _1, _2, and_1_out, and_2_out, and_3_out, and_4_out, and_5_out, clock_1_out, not_1_out, not_2_out,
       not_3_out, not_4_out, not_5_out, not_6_out, not_7_out, or_1_out, or_2_out;

  Clock clock_1 (.out(clock_1_out));
  not not_1 (not_1_out, _2);
  not not_2 (not_2_out, _1);
  not not_3 (not_3_out, _2);
  not not_4 (not_4_out, _1);
  not not_5 (not_5_out, _1);
  not not_6 (not_6_out, in_1);
  and and_1 (and_1_out, not_1_out, _1, in_1);
  and and_2 (and_2_out, not_2_out, _2);
  and and_3 (and_3_out, not_3_out, not_4_out, in_1);
  and and_4 (and_4_out, _2, not_5_out, not_6_out);
  and and_5 (and_5_out, _2, _1, in_1);
  not not_7 (not_7_out, in_1);
  or or_1 (or_1_out, and_1_out, and_2_out);
  or or_2 (or_2_out, and_3_out, and_4_out, and_5_out);
  and and_6 (out_2, _2, _1, not_7_out);
  D_Flip_Flop d_ff_1 (.clk(clock_1_out), .D(or_1_out), .Q(_2));  // open: Qn, preset, en, reset
  D_Flip_Flop d_ff_2 (.clk(clock_1_out), .D(or_2_out), .Q(_1));  // open: Qn, preset, en, reset
endmodule
