// Logisim project GUIA02.circ as structural Verilog: 1 circuit, main circuit main
module main (
  input  in_1,
  output out_2
);

  wire and_1_out, and_2_out, and_3_out, and_4_out, and_5_out, and_6_out, clock, not_1_out, not_2_out,
       not_3_out, not_4_out, not_5_out, not_6_out, not_7_out, not_8_out, not_9_out, not_10_out, not_11_out,
       not_12_out, not_13_out, not_14_out, not_15_out, or_1_out, or_2_out, Q0, Q1, Q2;

  Clock clock_1 (.out(clock));
  not not_1 (not_1_out, Q2);
  and and_1 (and_1_out, not_1_out, Q1, Q0, in_1);
  not not_2 (not_2_out, Q1);
  and and_2 (and_2_out, Q2, not_2_out, not_3_out, in_1);
  not not_3 (not_3_out, Q0);
  not not_4 (not_4_out, Q2);
  not not_5 (not_5_out, Q1);
  and and_3 (and_3_out, not_4_out, not_5_out, Q0, in_1);
  not not_6 (not_6_out, Q2);
  and and_4 (and_4_out, not_6_out, Q1, not_7_out);
  not not_7 (not_7_out, Q0);
  not not_8 (not_8_out, Q2);
  and and_5 (and_5_out, not_8_out, Q1, not_9_out, not_10_out);
  not not_9 (not_9_out, Q0);
  not not_10 (not_10_out, in_1);
  not not_11 (not_11_out, Q2);
  not not_12 (not_12_out, Q1);
  and and_6 (and_6_out, not_11_out, not_12_out, not_13_out, in_1);
  not not_13 (not_13_out, Q0);
  or or_1 (or_1_out, and_2_out, and_3_out, and_4_out);
  or or_2 (or_2_out, and_5_out, and_6_out);
  not not_14 (not_14_out, Q1);
  not not_15 (not_15_out, Q0);
  D_Flip_Flop d_ff_1 (.clk(clock), .D(and_1_out), .Q(Q2));  // open: Qn, preset, en, reset
  D_Flip_Flop d_ff_2 (.clk(clock), .D(or_1_out), .Q(Q1));  // open: Qn, preset, en, reset
  D_Flip_Flop d_ff_3 (.clk(clock), .D(or_2_out), .Q(Q0));  // open: Qn, preset, en, reset
  and and_7 (out_2, Q2, not_14_out, not_15_out, in_1);

  // Other names for the same wires on the sheet: x = in_1
endmodule
