// Logisim project GUIA03.circ as structural Verilog: 2 circuits, main circuit main
module Projeto (
  input  in_1
);

  wire and_1_out, clock_1_out, d_ff_1_q, d_ff_2_q, d_ff_3_q, d_ff_4_q, d_ff_4_qn, not_1_out;

  D_Flip_Flop d_ff_1 (.clk(clock_1_out), .D(in_1), .Q(d_ff_1_q));  // open: Qn, preset, en, reset
  Clock clock_1 (.out(clock_1_out));
  D_Flip_Flop d_ff_2 (.clk(clock_1_out), .D(d_ff_1_q), .Q(d_ff_2_q));  // open: Qn, preset, en, reset
  D_Flip_Flop d_ff_3 (.clk(clock_1_out), .D(d_ff_2_q), .Q(d_ff_3_q));  // open: Qn, preset, en, reset
  D_Flip_Flop d_ff_4 (.clk(clock_1_out), .D(d_ff_3_q), .Q(d_ff_4_q), .Qn(d_ff_4_qn));  // open: preset, en, reset
  not not_1 (not_1_out, d_ff_2_q);
  and and_1 (and_1_out, d_ff_4_q, d_ff_3_q, not_1_out, d_ff_1_q);
endmodule

module main (
  input  in_1,
  input  in_2,
  output out_3,
  output out_4
);

  wire _1, _2, and_1_out, and_2_out, and_3_out, and_4_out, and_5_out, and_6_out, and_7_out, and_8_out,
       and_9_out, and_10_out, and_11_out, clock, clock_1_out, not_1_out, not_2_out, not_3_out, not_4_out,
       not_5_out, not_6_out, not_7_out, not_8_out, not_9_out, not_10_out, not_11_out, not_12_out, not_13_out,
       not_14_out, not_15_out, not_16_out, not_17_out, not_18_out, not_19_out, not_20_out, not_21_out,
       not_22_out, or_1_out, or_2_out, or_3_out, or_4_out, Q0, Q1, Q2;

  Clock clock_1 (.out(clock_1_out));
  not not_1 (not_1_out, _2);
  not not_2 (not_2_out, _1);
  not not_3 (not_3_out, _2);
  not not_4 (not_4_out, _1);
  not not_5 (not_5_out, _1);
  not not_6 (not_6_out, in_1);
  and and_1 (and_1_out, not_1_out, _1, in_1);
  and and_2 (and_2_out, not_2_out, _2);
  and and_3 (and_3_out, not_3_out, not_4_out, in_1);
  and and_4 (and_4_out, _2, not_5_out, not_6_out);
  and and_5 (and_5_out, _2, _1, in_1);
  not not_7 (not_7_out, in_1);
  Clock clock_2 (.out(clock));
  not not_8 (not_8_out, Q2);
  and and_6 (and_6_out, not_8_out, Q1, Q0, in_2);
  not not_9 (not_9_out, Q1);
  and and_7 (and_7_out, Q2, not_9_out, not_10_out, in_2);
  not not_10 (not_10_out, Q0);
  not not_11 (not_11_out, Q2);
  not not_12 (not_12_out, Q1);
  and and_8 (and_8_out, not_11_out, not_12_out, Q0, in_2);
  not not_13 (not_13_out, Q2);
  and and_9 (and_9_out, not_13_out, Q1, not_14_out);
  not not_14 (not_14_out, Q0);
  not not_15 (not_15_out, Q2);
  and and_10 (and_10_out, not_15_out, Q1, not_16_out, not_17_out);
  not not_16 (not_16_out, Q0);
  not not_17 (not_17_out, in_2);
  not not_18 (not_18_out, Q2);
  not not_19 (not_19_out, Q1);
  and and_11 (and_11_out, not_18_out, not_19_out, not_20_out, in_2);
  not not_20 (not_20_out, Q0);
  or or_1 (or_1_out, and_1_out, and_2_out);
  or or_2 (or_2_out, and_3_out, and_4_out, and_5_out);
  and and_12 (out_3, _2, _1, not_7_out);
  or or_3 (or_3_out, and_7_out, and_8_out, and_9_out);
  or or_4 (or_4_out, and_10_out, and_11_out);
  D_Flip_Flop d_ff_1 (.clk(clock_1_out), .D(or_1_out), .Q(_2));  // open: Qn, preset, en, reset
  not not_21 (not_21_out, Q1);
  not not_22 (not_22_out, Q0);
  D_Flip_Flop d_ff_2 (.clk(clock_1_out), .D(or_2_out), .Q(_1));  // open: Qn, preset, en, reset
  and and_13 (out_4, Q2, not_21_out, not_22_out, in_2);
  D_Flip_Flop d_ff_3 (.clk(clock), .D(and_6_out), .Q(Q2));  // open: Qn, preset, en, reset
  D_Flip_Flop d_ff_4 (.clk(clock), .D(or_3_out), .Q(Q1));  // open: Qn, preset, en, reset
  D_Flip_Flop d_ff_5 (.clk(clock), .D(or_4_out), .Q(Q0));  // open: Qn, preset, en, reset

  // Other names for the same wires on the sheet: x = in_2

  // Notes on the sheet:
  //   MEALY
  //   MOORE
endmodule
