// Logisim project GUIA08.circ as structural Verilog: 1 circuit, main circuit main
module main (
  input  in_1,
  output out_2
);

  wire _00, _01, _10, and_1_out, and_2_out, clock_1_out, not_1_out, not_2_out, not_3_out;

  not not_1 (not_1_out, _00);
  not not_2 (not_2_out, _10);
  not not_3 (not_3_out, _01);
  Clock clock_1 (.out(clock_1_out));
  and and_1 (and_1_out, not_1_out, _01, not_2_out);
  or or_1 (out_2, and_1_out, and_2_out);
  and and_2 (and_2_out, _00, not_3_out, _10);
  D_Flip_Flop d_ff_1 (.clk(clock_1_out), .D(in_1), .Q(_00));  // open: Qn, preset, en, reset
  D_Flip_Flop d_ff_2 (.clk(clock_1_out), .D(_00), .Q(_01));  // open: Qn, preset, en, reset
  D_Flip_Flop d_ff_3 (.clk(clock_1_out), .D(_01), .Q(_10));  // open: Qn, preset, en, reset
endmodule
