// Logisim project Guia05_incompleto.circ as structural Verilog: 1 circuit, main circuit main
module main (
  input  in_1
);

  wire and_1_out, and_2_out, and_3_out, and_4_out, clock, not_1_out, not_2_out, not_3_out, not_4_out,
       not_5_out, not_6_out, or_1_out, or_2_out, Q0, Q1;

  not not_1 (not_1_out, Q0);
  not not_2 (not_2_out, in_1);
  not not_3 (not_3_out, Q1);
  not not_4 (not_4_out, in_1);
  not not_5 (not_5_out, Q0);
  not not_6 (not_6_out, in_1);
  // NOT_Gate not_7 has open pins: in=Q1, out=open
  // NOT_Gate not_8 has open pins: in=Q0, out=open
  Clock clock_1 (.out(clock));
  and and_1 (and_1_out, Q1, not_1_out, not_2_out);
  or or_1 (or_1_out, and_1_out, and_2_out);
  and and_2 (and_2_out, not_3_out, Q0, not_4_out);
  and and_3 (and_3_out, Q1, not_5_out, not_6_out);
  buf and_4 (and_4_out, in_1);  // AND_Gate
  or or_2 (or_2_out, and_3_out, and_4_out);
  D_Flip_Flop d_ff_1 (.clk(clock), .D(or_1_out), .Q(Q1));  // open: Qn, preset, en, reset
  D_Flip_Flop d_ff_2 (.clk(clock), .D(or_2_out), .Q(Q0));  // open: Qn, preset, en, reset

  // Other names for the same wires on the sheet: x = in_1
endmodule
