// Logisim project Exericio02.circ as structural Verilog: 3 circuits, main circuit main
module main (
  input  [7:0] in_1,
  input  in_2,
  input  in_3,
  input  in_4,
  output [7:0] out_5
);

  wire clock_1_out;

  Clock clock_1 (.out(clock_1_out));
  _1x4 u_1x4_1 (
    .clock(clock_1_out), .entrada(in_1[7:4]), .\endereço (in_2), .saida(out_5[7:4]), .in_4(in_3), .in_5(in_4));  // open: saida_negada
  RAM_1x2 ram_1x2_1 (
    .clock(clock_1_out), .entrada(in_1[3:2]), .out_6(out_5[3:2]), .ligar(in_3), .limpar(in_4),
    .\endereço (in_2));  // open: out_7
  RAM_1x2 ram_1x2_2 (
    .clock(clock_1_out), .entrada(in_1[1:0]), .out_6(out_5[1:0]), .ligar(in_3), .limpar(in_4),
    .\endereço (in_2));  // open: out_7
endmodule

module RAM_1x2 (
  input  clock,
  input  [1:0] entrada,
  input  \endereço ,
  input  ligar,
  input  limpar,
  output [1:0] out_6,
  output [1:0] out_7
);

  J_K_Flip_Flop j_k_ff_1 (
    .J(entrada[1]), .clk(clock), .K(\endereço ), .Q(out_6[1]), .en(ligar), .reset(limpar));  // open: Qn, preset
  J_K_Flip_Flop j_k_ff_2 (
    .J(entrada[0]), .clk(clock), .K(\endereço ), .Q(out_6[0]), .en(ligar), .reset(limpar));  // open: Qn, preset
  assign out_7 = ~out_6;  // NOT_Gate not_1, 2 bits wide
endmodule

module _1x4 (
  input  clock,
  input  [3:0] entrada,
  input  \endereço ,
  input  in_4,
  input  in_5,
  output [3:0] saida,
  output [3:0] saida_negada
);

  RAM_1x2 ram_1x2_1 (
    .clock(clock), .entrada(entrada[3:2]), .out_6(saida[3:2]), .ligar(in_4), .limpar(in_5),
    .\endereço (\endereço ));  // open: out_7
  RAM_1x2 ram_1x2_2 (
    .clock(clock), .entrada(entrada[1:0]), .out_6(saida[1:0]), .ligar(in_4), .limpar(in_5),
    .\endereço (\endereço ));  // open: out_7
  assign saida_negada = ~saida;  // NOT_Gate not_1, 4 bits wide
endmodule
