// Logisim project Exericio03.circ as structural Verilog: 4 circuits, main circuit main
module main (
  input  in_1,
  input  [7:0] in_2,
  input  in_3,
  output [7:0] out_4
);

  wire clk, mymultiplexador_1_out_2, mymultiplexador_1_out_3, not_1_out, not_2_out, not_3_out, not_4_out;
  wire [3:0] n1x4_1_saida, n1x4_2_saida, n1x4_3_saida, n1x4_4_saida;

  Clock clock_1 (.out(clk));
  MyMultiplexador mymultiplexador_1 (.out_2(mymultiplexador_1_out_2), .out_3(mymultiplexador_1_out_3), .in_1(in_3));
  _1x4 u_1x4_1 (
    .clock(clk), .entrada(in_2[3:0]), .ligar(not_1_out), .saida(n1x4_1_saida),
    .\endereço (mymultiplexador_1_out_2), .clear(in_1));  // open: saida_negada
  not not_1 (not_1_out, clk);
  _1x4 u_1x4_2 (
    .clock(clk), .entrada(in_2[3:0]), .ligar(not_2_out), .saida(n1x4_2_saida),
    .\endereço (mymultiplexador_1_out_3), .clear(in_1));  // open: saida_negada
  not not_2 (not_2_out, clk);
  _1x4 u_1x4_3 (
    .clock(clk), .entrada(in_2[7:4]), .ligar(not_3_out), .saida(n1x4_3_saida),
    .\endereço (mymultiplexador_1_out_2), .clear(in_1));  // open: saida_negada
  not not_3 (not_3_out, clk);
  _1x4 u_1x4_4 (
    .clock(clk), .entrada(in_2[7:4]), .ligar(not_4_out), .saida(n1x4_4_saida),
    .\endereço (mymultiplexador_1_out_3), .clear(in_1));  // open: saida_negada
  not not_4 (not_4_out, clk);
  assign out_4 = {n1x4_3_saida, n1x4_1_saida} | {n1x4_4_saida, n1x4_2_saida};  // OR_Gate or_1, 8 bits wide

  // Other names for the same wires on the sheet: E2[3:0] = in_2[7:4]; E1[3:0] = in_2[3:0]
endmodule

module RAM_1x2 (
  input  clock,
  input  [1:0] entrada,
  input  ligar,
  input  \endereço ,
  input  limpar,
  output [1:0] out_6,
  output [1:0] out_7
);

  wire j_k_ff_1_q, j_k_ff_2_q;

  J_K_Flip_Flop j_k_ff_1 (
    .J(entrada[1]), .clk(clock), .K(ligar), .Q(j_k_ff_1_q), .en(\endereço ), .reset(limpar));  // open: Qn, preset
  J_K_Flip_Flop j_k_ff_2 (
    .J(entrada[0]), .clk(clock), .K(ligar), .Q(j_k_ff_2_q), .en(\endereço ), .reset(limpar));  // open: Qn, preset
  and and_1 (out_6[0], j_k_ff_2_q, \endereço );
  and and_2 (out_6[1], j_k_ff_1_q, \endereço );
  assign out_7 = ~out_6;  // NOT_Gate not_1, 2 bits wide
endmodule

module _1x4 (
  input  clock,
  input  [3:0] entrada,
  input  ligar,
  input  \endereço ,
  input  clear,
  output [3:0] saida,
  output [3:0] saida_negada
);

  RAM_1x2 ram_1x2_1 (
    .clock(clock), .entrada(entrada[3:2]), .out_6(saida[3:2]), .\endereço (\endereço ), .limpar(clear),
    .ligar(ligar));  // open: out_7
  RAM_1x2 ram_1x2_2 (
    .clock(clock), .entrada(entrada[1:0]), .out_6(saida[1:0]), .\endereço (\endereço ), .limpar(clear),
    .ligar(ligar));  // open: out_7
  assign saida_negada = ~saida;  // NOT_Gate not_1, 4 bits wide
endmodule

module MyMultiplexador (
  input  in_1,
  output out_2,
  output out_3
);

  wire not_1_out;

  and and_1 (out_2, in_1, 1'b1);
  not not_1 (not_1_out, in_1);
  and and_2 (out_3, not_1_out, 1'b1);
endmodule
