// Logisim project Exericio04.circ as structural Verilog: 7 circuits, main circuit main
module main (
  input  [7:0] entrada,
  input  [1:0] endere,
  input  clear,
  output [7:0] out_4
);

  wire clk_out, demultiplexer_1_out0, demultiplexer_1_out1, mymultiplexador_1_out_2, mymultiplexador_1_out_3;
  wire [3:0] n2x4_1_saida, n2x4_2_saida, n2x4_3_saida, n2x4_4_saida;

  Demultiplexer demultiplexer_1 (
    .out0(demultiplexer_1_out0), .out1(demultiplexer_1_out1), .in(clk_out), .sel(endere[1]));  // open: en
  Clock clk (.out(clk_out));
  MyMultiplexador mymultiplexador_1 (
    .out_2(mymultiplexador_1_out_2), .out_3(mymultiplexador_1_out_3), .in_1(endere[0]));
  _2x4 u_2x4_1 (
    .clk(demultiplexer_1_out0), .entrada(entrada[3:0]), .saida(n2x4_1_saida), .clear(clear),
    .endere(mymultiplexador_1_out_2));  // open: saida_negada
  _2x4 u_2x4_2 (
    .clk(demultiplexer_1_out1), .entrada(entrada[3:0]), .saida(n2x4_2_saida), .clear(clear),
    .endere(mymultiplexador_1_out_3));  // open: saida_negada
  _2x4 u_2x4_3 (
    .clk(demultiplexer_1_out0), .entrada(entrada[7:4]), .saida(n2x4_3_saida), .clear(clear),
    .endere(mymultiplexador_1_out_2));  // open: saida_negada
  _2x4 u_2x4_4 (
    .clk(demultiplexer_1_out1), .entrada(entrada[7:4]), .saida(n2x4_4_saida), .clear(clear),
    .endere(mymultiplexador_1_out_3));  // open: saida_negada
  Multiplexer #(.width(8)) multiplexer_1 (
    .in0({n2x4_3_saida, n2x4_1_saida}), .in1({n2x4_4_saida, n2x4_2_saida}), .out(out_4), .sel(endere[1]));  // open: en
endmodule

module RAM_1x2 (
  input  clock,
  input  [1:0] entrada,
  input  ligar,
  input  \endereço ,
  input  limpar,
  output [1:0] out_6,
  output [1:0] out_7
);

  wire j_k_ff_1_q, j_k_ff_2_q;

  J_K_Flip_Flop j_k_ff_1 (
    .J(entrada[1]), .clk(clock), .K(ligar), .Q(j_k_ff_1_q), .en(\endereço ), .reset(limpar));  // open: Qn, preset
  J_K_Flip_Flop j_k_ff_2 (
    .J(entrada[0]), .clk(clock), .K(ligar), .Q(j_k_ff_2_q), .en(\endereço ), .reset(limpar));  // open: Qn, preset
  and and_1 (out_6[0], j_k_ff_2_q, \endereço );
  and and_2 (out_6[1], j_k_ff_1_q, \endereço );
  assign out_7 = ~out_6;  // NOT_Gate not_1, 2 bits wide
endmodule

module _1x4 (
  input  clock,
  input  [3:0] entrada,
  input  ligar,
  input  \endereço ,
  input  clear,
  output [3:0] saida,
  output [3:0] saida_negada
);

  RAM_1x2 ram_1x2_1 (
    .clock(clock), .entrada(entrada[3:2]), .out_6(saida[3:2]), .\endereço (\endereço ), .limpar(clear),
    .ligar(ligar));  // open: out_7
  RAM_1x2 ram_1x2_2 (
    .clock(clock), .entrada(entrada[1:0]), .out_6(saida[1:0]), .\endereço (\endereço ), .limpar(clear),
    .ligar(ligar));  // open: out_7
  assign saida_negada = ~saida;  // NOT_Gate not_1, 4 bits wide
endmodule

module MyMultiplexador (
  input  in_1,
  output out_2,
  output out_3
);

  wire not_1_out;

  and and_1 (out_2, in_1, 1'b1);
  not not_1 (not_1_out, in_1);
  and and_2 (out_3, not_1_out, 1'b1);
endmodule

module _2x4 (
  input  clk,
  input  [3:0] entrada,
  input  endere,
  input  clear,
  output [3:0] saida,
  output [3:0] saida_negada
);

  wire mymultiplexador_1_out_2, mymultiplexador_1_out_3, not_1_out, not_2_out;
  wire [3:0] n1x4_1_saida, n1x4_2_saida;

  not not_1 (not_1_out, clk);
  MyMultiplexador mymultiplexador_1 (.out_2(mymultiplexador_1_out_2), .out_3(mymultiplexador_1_out_3), .in_1(endere));
  not not_2 (not_2_out, clk);
  _1x4 u_1x4_1 (
    .clock(clk), .entrada(entrada), .saida(n1x4_1_saida), .ligar(not_1_out),
    .\endereço (mymultiplexador_1_out_2), .clear(clear));  // open: saida_negada
  _1x4 u_1x4_2 (
    .clock(clk), .entrada(entrada), .saida(n1x4_2_saida), .ligar(not_2_out),
    .\endereço (mymultiplexador_1_out_3), .clear(clear));  // open: saida_negada
  assign saida = n1x4_1_saida | n1x4_2_saida;  // OR_Gate or_1, 4 bits wide
  assign saida_negada = ~saida;  // NOT_Gate not_3, 4 bits wide
endmodule

module mux_4 (
  input  [1:0] in_1,
  output out_2,
  output out_3,
  output out_4,
  output out_5
);

  wire not_1_out, not_2_out, not_3_out, not_4_out;

  not not_1 (not_1_out, in_1[0]);
  and and_1 (out_2, not_1_out, not_2_out);
  not not_2 (not_2_out, in_1[1]);
  and and_2 (out_3, in_1[0], not_3_out);
  not not_3 (not_3_out, in_1[1]);
  not not_4 (not_4_out, in_1[0]);
  and and_3 (out_4, not_4_out, in_1[1]);
  and and_4 (out_5, in_1[0], in_1[1]);
endmodule

module _4x8 (
  input  [7:0] entrada,
  input  [1:0] endere,
  input  clear,
  output [7:0] out_4
);

  wire clk_out, demultiplexer_1_out0, demultiplexer_1_out1, mymultiplexador_1_out_2, mymultiplexador_1_out_3;
  wire [3:0] n2x4_1_saida, n2x4_2_saida, n2x4_3_saida, n2x4_4_saida;

  Demultiplexer demultiplexer_1 (
    .out0(demultiplexer_1_out0), .out1(demultiplexer_1_out1), .in(clk_out), .sel(endere[1]));  // open: en
  Clock clk (.out(clk_out));
  MyMultiplexador mymultiplexador_1 (
    .out_2(mymultiplexador_1_out_2), .out_3(mymultiplexador_1_out_3), .in_1(endere[0]));
  _2x4 u_2x4_1 (
    .clk(demultiplexer_1_out0), .entrada(entrada[3:0]), .saida(n2x4_1_saida), .clear(clear),
    .endere(mymultiplexador_1_out_2));  // open: saida_negada
  _2x4 u_2x4_2 (
    .clk(demultiplexer_1_out1), .entrada(entrada[3:0]), .saida(n2x4_2_saida), .clear(clear),
    .endere(mymultiplexador_1_out_3));  // open: saida_negada
  _2x4 u_2x4_3 (
    .clk(demultiplexer_1_out0), .entrada(entrada[7:4]), .saida(n2x4_3_saida), .clear(clear),
    .endere(mymultiplexador_1_out_2));  // open: saida_negada
  _2x4 u_2x4_4 (
    .clk(demultiplexer_1_out1), .entrada(entrada[7:4]), .saida(n2x4_4_saida), .clear(clear),
    .endere(mymultiplexador_1_out_3));  // open: saida_negada
  Multiplexer #(.width(8)) multiplexer_1 (
    .in0({n2x4_3_saida, n2x4_1_saida}), .in1({n2x4_4_saida, n2x4_2_saida}), .out(out_4), .sel(endere[1]));  // open: en
endmodule
