// Logisim project Exericio06.circ as structural Verilog: 8 circuits, main circuit main
module main (
  input  [15:0] in_1,
  input  [1:0] in_2,
  input  in_3,
  output [15:0] out_4
);

  wire clock_1_out;

  Clock clock_1 (.out(clock_1_out));
  _4x8 u_4x8_1 (.entrada(in_1[15:8]), .out_5(out_4[15:8]), .endere(in_2), .clear(in_3), .clk(clock_1_out));
  _4x8 u_4x8_2 (.entrada(in_1[7:0]), .out_5(out_4[7:0]), .endere(in_2), .clear(in_3), .clk(clock_1_out));
endmodule

module RAM_1x2 (
  input  clock,
  input  [1:0] entrada,
  input  ligar,
  input  \endereço ,
  input  limpar,
  output [1:0] out_6,
  output [1:0] out_7
);

  wire j_k_ff_1_q, j_k_ff_2_q;

  J_K_Flip_Flop j_k_ff_1 (
    .J(entrada[1]), .clk(clock), .K(ligar), .Q(j_k_ff_1_q), .en(\endereço ), .reset(limpar));  // open: Qn, preset
  J_K_Flip_Flop j_k_ff_2 (
    .J(entrada[0]), .clk(clock), .K(ligar), .Q(j_k_ff_2_q), .en(\endereço ), .reset(limpar));  // open: Qn, preset
  and and_1 (out_6[0], j_k_ff_2_q, \endereço );
  and and_2 (out_6[1], j_k_ff_1_q, \endereço );
  assign out_7 = ~out_6;  // NOT_Gate not_1, 2 bits wide
endmodule

module _1x4 (
  input  clock,
  input  [3:0] entrada,
  input  ligar,
  input  \endereço ,
  input  clear,
  output [3:0] saida,
  output [3:0] saida_negada
);

  RAM_1x2 ram_1x2_1 (
    .clock(clock), .entrada(entrada[3:2]), .out_6(saida[3:2]), .\endereço (\endereço ), .limpar(clear),
    .ligar(ligar));  // open: out_7
  RAM_1x2 ram_1x2_2 (
    .clock(clock), .entrada(entrada[1:0]), .out_6(saida[1:0]), .\endereço (\endereço ), .limpar(clear),
    .ligar(ligar));  // open: out_7
  assign saida_negada = ~saida;  // NOT_Gate not_1, 4 bits wide
endmodule

module MyMultiplexador (
  input  in_1,
  output out_2,
  output out_3
);

  wire not_1_out;

  and and_1 (out_2, in_1, 1'b1);
  not not_1 (not_1_out, in_1);
  and and_2 (out_3, not_1_out, 1'b1);
endmodule

module _2x4 (
  input  clk,
  input  [3:0] entrada,
  input  endere,
  input  clear,
  output [3:0] saida,
  output [3:0] saida_negada
);

  wire mymultiplexador_1_out_2, mymultiplexador_1_out_3, not_1_out, not_2_out;
  wire [3:0] n1x4_1_saida, n1x4_2_saida;

  not not_1 (not_1_out, clk);
  MyMultiplexador mymultiplexador_1 (.out_2(mymultiplexador_1_out_2), .out_3(mymultiplexador_1_out_3), .in_1(endere));
  not not_2 (not_2_out, clk);
  _1x4 u_1x4_1 (
    .clock(clk), .entrada(entrada), .saida(n1x4_1_saida), .ligar(not_1_out),
    .\endereço (mymultiplexador_1_out_2), .clear(clear));  // open: saida_negada
  _1x4 u_1x4_2 (
    .clock(clk), .entrada(entrada), .saida(n1x4_2_saida), .ligar(not_2_out),
    .\endereço (mymultiplexador_1_out_3), .clear(clear));  // open: saida_negada
  assign saida = n1x4_1_saida | n1x4_2_saida;  // OR_Gate or_1, 4 bits wide
  assign saida_negada = ~saida;  // NOT_Gate not_3, 4 bits wide
endmodule

module mux_4 (
  input  [1:0] in_1,
  output out_2,
  output out_3,
  output out_4,
  output out_5
);

  wire not_1_out, not_2_out, not_3_out, not_4_out;

  not not_1 (not_1_out, in_1[0]);
  and and_1 (out_2, not_1_out, not_2_out);
  not not_2 (not_2_out, in_1[1]);
  and and_2 (out_3, in_1[0], not_3_out);
  not not_3 (not_3_out, in_1[1]);
  not not_4 (not_4_out, in_1[0]);
  and and_3 (out_4, not_4_out, in_1[1]);
  and and_4 (out_5, in_1[0], in_1[1]);
endmodule

module _4x8 (
  input  [7:0] entrada,
  input  clk,
  input  [1:0] endere,
  input  clear,
  output [7:0] out_5
);

  wire demultiplexer_1_out0, demultiplexer_1_out1, mymultiplexador_1_out_2, mymultiplexador_1_out_3;
  wire [3:0] n2x4_1_saida, n2x4_2_saida, n2x4_3_saida, n2x4_4_saida;

  Demultiplexer demultiplexer_1 (
    .out0(demultiplexer_1_out0), .out1(demultiplexer_1_out1), .in(clk), .sel(endere[1]));  // open: en
  MyMultiplexador mymultiplexador_1 (
    .out_2(mymultiplexador_1_out_2), .out_3(mymultiplexador_1_out_3), .in_1(endere[0]));
  _2x4 u_2x4_1 (
    .clk(demultiplexer_1_out0), .entrada(entrada[3:0]), .saida(n2x4_1_saida), .clear(clear),
    .endere(mymultiplexador_1_out_2));  // open: saida_negada
  _2x4 u_2x4_2 (
    .clk(demultiplexer_1_out1), .entrada(entrada[3:0]), .saida(n2x4_2_saida), .clear(clear),
    .endere(mymultiplexador_1_out_3));  // open: saida_negada
  _2x4 u_2x4_3 (
    .clk(demultiplexer_1_out0), .entrada(entrada[7:4]), .saida(n2x4_3_saida), .clear(clear),
    .endere(mymultiplexador_1_out_2));  // open: saida_negada
  _2x4 u_2x4_4 (
    .clk(demultiplexer_1_out1), .entrada(entrada[7:4]), .saida(n2x4_4_saida), .clear(clear),
    .endere(mymultiplexador_1_out_3));  // open: saida_negada
  Multiplexer #(.width(8)) multiplexer_1 (
    .in0({n2x4_3_saida, n2x4_1_saida}), .in1({n2x4_4_saida, n2x4_2_saida}), .out(out_5), .sel(endere[1]));  // open: en
endmodule

module _8x8 (
  input  [7:0] in_1,
  input  [2:0] adress,
  input  in_3,
  output [7:0] out_4
);

  wire clock_1_out, demultiplexer_1_out0, demultiplexer_1_out1;
  wire [7:0] n4x8_1_out_5, n4x8_2_out_5;

  Clock clock_1 (.out(clock_1_out));
  Demultiplexer demultiplexer_1 (
    .out0(demultiplexer_1_out0), .out1(demultiplexer_1_out1), .in(clock_1_out), .sel(adress[2]));  // open: en
  _4x8 u_4x8_1 (.entrada(in_1), .out_5(n4x8_1_out_5), .endere(adress[1:0]), .clear(in_3), .clk(demultiplexer_1_out0));
  _4x8 u_4x8_2 (.entrada(in_1), .out_5(n4x8_2_out_5), .endere(adress[1:0]), .clear(in_3), .clk(demultiplexer_1_out1));
  Multiplexer #(.width(8)) multiplexer_1 (
    .in0(n4x8_1_out_5), .in1(n4x8_2_out_5), .out(out_4), .sel(adress[2]));  // open: en
endmodule
