// Logisim project Exericio07.circ as structural Verilog: 7 circuits, main circuit main
module main (
  input  [2:0] in_1,
  input  [15:0] in_2,
  input  in_3,
  output [15:0] out_4
);

  wire clock_1_out, mux_1_out_2, mux_1_out_3, mux_1_out_4, mux_1_out_5, mux_1_out_6, mux_1_out_7,
       mux_1_out_8, mux_1_out_9;
  wire [15:0] n1x16_1_out_5, n1x16_2_out_5, n1x16_3_out_5, n1x16_4_out_5, n1x16_5_out_5, n1x16_6_out_5,
       n1x16_7_out_5, n1x16_8_out_5;

  Clock clock_1 (.out(clock_1_out));
  mux mux_1 (
    .in_1(in_1), .out_2(mux_1_out_2), .out_3(mux_1_out_3), .out_4(mux_1_out_4), .out_5(mux_1_out_5),
    .out_6(mux_1_out_6), .out_7(mux_1_out_7), .out_8(mux_1_out_8), .out_9(mux_1_out_9));
  _1x16 u_1x16_1 (.clk(clock_1_out), .entrada(in_2), .\endereço (mux_1_out_2), .out_5(n1x16_1_out_5), .clear(in_3));
  _1x16 u_1x16_2 (.clk(clock_1_out), .entrada(in_2), .\endereço (mux_1_out_6), .out_5(n1x16_2_out_5), .clear(in_3));
  _1x16 u_1x16_3 (.clk(clock_1_out), .entrada(in_2), .\endereço (mux_1_out_3), .out_5(n1x16_3_out_5), .clear(in_3));
  _1x16 u_1x16_4 (.clk(clock_1_out), .entrada(in_2), .\endereço (mux_1_out_7), .out_5(n1x16_4_out_5), .clear(in_3));
  _1x16 u_1x16_5 (.clk(clock_1_out), .entrada(in_2), .\endereço (mux_1_out_4), .out_5(n1x16_5_out_5), .clear(in_3));
  _1x16 u_1x16_6 (.clk(clock_1_out), .entrada(in_2), .\endereço (mux_1_out_8), .out_5(n1x16_6_out_5), .clear(in_3));
  _1x16 u_1x16_7 (.clk(clock_1_out), .entrada(in_2), .\endereço (mux_1_out_5), .out_5(n1x16_7_out_5), .clear(in_3));
  _1x16 u_1x16_8 (.clk(clock_1_out), .entrada(in_2), .\endereço (mux_1_out_9), .out_5(n1x16_8_out_5), .clear(in_3));
  assign out_4 = n1x16_7_out_5 | n1x16_8_out_5 | n1x16_5_out_5 | n1x16_6_out_5 | n1x16_3_out_5 | n1x16_4_out_5 | n1x16_1_out_5 | n1x16_2_out_5;  // OR_Gate or_1, 16 bits wide
endmodule

module RAM_1x2 (
  input  clock,
  input  [1:0] entrada,
  input  ligar,
  input  \endereço ,
  input  limpar,
  output [1:0] out_6,
  output [1:0] out_7
);

  wire j_k_ff_1_q, j_k_ff_2_q;

  J_K_Flip_Flop j_k_ff_1 (
    .J(entrada[1]), .clk(clock), .K(ligar), .Q(j_k_ff_1_q), .en(\endereço ), .reset(limpar));  // open: Qn, preset
  J_K_Flip_Flop j_k_ff_2 (
    .J(entrada[0]), .clk(clock), .K(ligar), .Q(j_k_ff_2_q), .en(\endereço ), .reset(limpar));  // open: Qn, preset
  and and_1 (out_6[0], j_k_ff_2_q, \endereço );
  and and_2 (out_6[1], j_k_ff_1_q, \endereço );
  assign out_7 = ~out_6;  // NOT_Gate not_1, 2 bits wide
endmodule

module _1x4 (
  input  clock,
  input  [3:0] entrada,
  input  \endereço ,
  input  clear,
  output [3:0] saida,
  output [3:0] saida_negada
);

  wire not_1_out, not_2_out;

  RAM_1x2 ram_1x2_1 (
    .clock(clock), .entrada(entrada[3:2]), .out_6(saida[3:2]), .\endereço (\endereço ), .limpar(clear),
    .ligar(not_1_out));  // open: out_7
  not not_1 (not_1_out, clock);
  RAM_1x2 ram_1x2_2 (
    .clock(clock), .entrada(entrada[1:0]), .out_6(saida[1:0]), .\endereço (\endereço ), .limpar(clear),
    .ligar(not_2_out));  // open: out_7
  not not_2 (not_2_out, clock);
  assign saida_negada = ~saida;  // NOT_Gate not_3, 4 bits wide
endmodule

module MyMultiplexador (
  input  in_1,
  output out_2,
  output out_3
);

  wire not_1_out;

  and and_1 (out_2, in_1, 1'b1);
  not not_1 (not_1_out, in_1);
  and and_2 (out_3, not_1_out, 1'b1);
endmodule

module _2x4 (
  input  clk,
  input  [3:0] entrada,
  input  endere,
  input  clear,
  output [3:0] saida,
  output [3:0] saida_negada
);

  wire mymultiplexador_1_out_2, mymultiplexador_1_out_3, not_1_out, not_2_out;
  wire [3:0] n1x4_1_p6, n1x4_2_p6;

  not not_1 (not_1_out, clk);
  MyMultiplexador mymultiplexador_1 (.out_2(mymultiplexador_1_out_2), .out_3(mymultiplexador_1_out_3), .in_1(endere));
  not not_2 (not_2_out, clk);
  // _1x4 1x4_1: pin names not known; wires that end beside it: clk, entrada, not_1_out, mymultiplexador_1_out_2, clear, n1x4_1_p6
  // _1x4 1x4_2: pin names not known; wires that end beside it: clk, entrada, not_2_out, mymultiplexador_1_out_3, clear, n1x4_2_p6
  assign saida = n1x4_1_p6 | n1x4_2_p6;  // OR_Gate or_1, 4 bits wide
  assign saida_negada = ~saida;  // NOT_Gate not_3, 4 bits wide
endmodule

module _1x16 (
  input  clk,
  input  [15:0] entrada,
  input  \endereço ,
  input  clear,
  output [15:0] out_5
);

  _1x4 u_1x4_1 (
    .clock(clk), .entrada(entrada[3:0]), .saida(out_5[3:0]), .\endereço (\endereço ), .clear(clear));  // open: saida_negada
  _1x4 u_1x4_2 (
    .clock(clk), .entrada(entrada[7:4]), .saida(out_5[7:4]), .\endereço (\endereço ), .clear(clear));  // open: saida_negada
  _1x4 u_1x4_3 (
    .clock(clk), .entrada(entrada[11:8]), .saida(out_5[11:8]), .\endereço (\endereço ), .clear(clear));  // open: saida_negada
  _1x4 u_1x4_4 (
    .clock(clk), .entrada(entrada[15:12]), .saida(out_5[15:12]), .\endereço (\endereço ), .clear(clear));  // open: saida_negada
endmodule

module mux (
  input  [2:0] in_1,
  output out_2,
  output out_3,
  output out_4,
  output out_5,
  output out_6,
  output out_7,
  output out_8,
  output out_9
);

  wire not_1_out, not_2_out, not_3_out, not_4_out, not_5_out, not_6_out, not_7_out, not_8_out, not_9_out,
       not_10_out, not_11_out, not_12_out;

  not not_1 (not_1_out, in_1[0]);
  not not_2 (not_2_out, in_1[1]);
  and and_1 (out_2, not_1_out, not_2_out, not_3_out);
  not not_3 (not_3_out, in_1[2]);
  and and_2 (out_3, in_1[0], not_4_out, not_5_out);
  not not_4 (not_4_out, in_1[1]);
  not not_5 (not_5_out, in_1[2]);
  not not_6 (not_6_out, in_1[0]);
  and and_3 (out_4, not_6_out, in_1[1], not_7_out);
  not not_7 (not_7_out, in_1[2]);
  and and_4 (out_5, in_1[0], in_1[1], not_8_out);
  not not_8 (not_8_out, in_1[2]);
  not not_9 (not_9_out, in_1[0]);
  not not_10 (not_10_out, in_1[1]);
  and and_5 (out_6, not_9_out, not_10_out, in_1[2]);
  and and_6 (out_7, in_1[0], not_11_out, in_1[2]);
  not not_11 (not_11_out, in_1[1]);
  not not_12 (not_12_out, in_1[0]);
  and and_7 (out_8, not_12_out, in_1[1], in_1[2]);
  and and_8 (out_9, in_1[0], in_1[1], in_1[2]);
endmodule
