// Logisim project Exercicio01.circ as structural Verilog: 1 circuit, main circuit main
module main (
  input  clk,
  input  in_2,
  input  clear,
  output [4:0] out_4
);

  J_K_Flip_Flop j_k_ff_1 (.J(in_2), .clk(clk), .K(in_2), .Q(out_4[0]), .en(in_2), .reset(clear));  // open: Qn, preset
  J_K_Flip_Flop j_k_ff_2 (
    .J(in_2), .clk(out_4[0]), .K(in_2), .Q(out_4[1]), .en(in_2), .reset(clear));  // open: Qn, preset
  J_K_Flip_Flop j_k_ff_3 (
    .J(in_2), .clk(out_4[1]), .K(in_2), .Q(out_4[2]), .en(in_2), .reset(clear));  // open: Qn, preset
  J_K_Flip_Flop j_k_ff_4 (
    .J(in_2), .clk(out_4[2]), .K(in_2), .Q(out_4[3]), .en(in_2), .reset(clear));  // open: Qn, preset
  J_K_Flip_Flop j_k_ff_5 (
    .J(in_2), .clk(out_4[3]), .K(in_2), .Q(out_4[4]), .en(in_2), .reset(clear));  // open: Qn, preset
endmodule
