// Logisim project Exercicio02.circ as structural Verilog: 1 circuit, main circuit main
module main (
  input  clk,
  input  in_2,
  input  clear,
  output [4:0] out_4
);

  wire j_k_ff_1_qn, j_k_ff_2_qn, j_k_ff_3_qn, j_k_ff_4_qn;

  J_K_Flip_Flop j_k_ff_1 (
    .J(in_2), .clk(clk), .K(in_2), .Q(out_4[0]), .Qn(j_k_ff_1_qn), .en(in_2), .reset(clear));  // open: preset
  J_K_Flip_Flop j_k_ff_2 (
    .J(in_2), .clk(j_k_ff_1_qn), .K(in_2), .Q(out_4[1]), .Qn(j_k_ff_2_qn), .en(in_2), .reset(clear));  // open: preset
  J_K_Flip_Flop j_k_ff_3 (
    .J(in_2), .clk(j_k_ff_2_qn), .K(in_2), .Q(out_4[2]), .Qn(j_k_ff_3_qn), .en(in_2), .reset(clear));  // open: preset
  J_K_Flip_Flop j_k_ff_4 (
    .J(in_2), .clk(j_k_ff_3_qn), .K(in_2), .Q(out_4[3]), .Qn(j_k_ff_4_qn), .en(in_2), .reset(clear));  // open: preset
  J_K_Flip_Flop j_k_ff_5 (
    .J(in_2), .clk(j_k_ff_4_qn), .K(in_2), .Q(out_4[4]), .en(in_2), .reset(clear));  // open: Qn, preset
endmodule
