// Logisim project Exercicio04.circ as structural Verilog: 1 circuit, main circuit main
module main (
  input  in_1,
  input  clear,
  output out_3,
  output out_4,
  output out_5,
  output out_6
);

  wire clock_1_out, j_k_ff_1_qn, j_k_ff_2_qn, j_k_ff_4_qn, nand_1_out, nand_2_out, not_1_out;

  Clock clock_1 (.out(clock_1_out));
  nand nand_1 (nand_1_out, clear, nand_2_out);
  nand nand_2 (nand_2_out, out_3, out_4, out_5, not_1_out);
  not not_1 (not_1_out, out_6);
  J_K_Flip_Flop j_k_ff_1 (
    .J(in_1), .clk(clock_1_out), .K(in_1), .Q(out_6), .Qn(j_k_ff_1_qn), .reset(nand_1_out));  // open: preset, en
  J_K_Flip_Flop j_k_ff_2 (
    .J(in_1), .clk(j_k_ff_1_qn), .K(in_1), .Q(out_5), .Qn(j_k_ff_2_qn), .reset(nand_1_out));  // open: preset, en
  J_K_Flip_Flop j_k_ff_3 (
    .J(in_1), .clk(j_k_ff_4_qn), .K(in_1), .Q(out_3), .reset(nand_1_out));  // open: Qn, preset, en
  J_K_Flip_Flop j_k_ff_4 (
    .J(in_1), .clk(j_k_ff_2_qn), .K(in_1), .Q(out_4), .Qn(j_k_ff_4_qn), .reset(nand_1_out));  // open: preset, en
endmodule
