// Logisim project Exercicio05.circ as structural Verilog: 1 circuit, main circuit main
module main (
  input  in_1,
  input  clear,
  output out_3,
  output out_4,
  output out_5,
  output out_6
);

  wire and_1_out, and_2_out, and_3_out, clock_1_out, not_1_out, t_ff_1_qn, t_ff_2_qn, t_ff_4_qn;

  Clock clock_1 (.out(clock_1_out));
  T_Flip_Flop t_ff_1 (.clk(clock_1_out), .T(in_1), .Q(out_6), .Qn(t_ff_1_qn), .preset(clear));  // open: reset, en
  and and_1 (and_1_out, t_ff_1_qn, not_1_out);
  not not_1 (not_1_out, clear);
  T_Flip_Flop t_ff_2 (.clk(clock_1_out), .T(and_1_out), .Q(out_5), .Qn(t_ff_2_qn), .preset(clear));  // open: reset, en
  and and_2 (and_2_out, t_ff_2_qn, and_1_out);
  T_Flip_Flop t_ff_3 (.clk(clock_1_out), .T(and_3_out), .Q(out_3), .preset(clear));  // open: Qn, reset, en
  T_Flip_Flop t_ff_4 (.clk(clock_1_out), .T(and_2_out), .Q(out_4), .Qn(t_ff_4_qn), .preset(clear));  // open: reset, en
  and and_3 (and_3_out, t_ff_4_qn, and_2_out);
endmodule
