// Logisim project Exercicio03.circ as structural Verilog: 1 circuit, main circuit main
module main (
  input  in_1,
  input  clear,
  output out_3,
  output out_4,
  output out_5,
  output out_6,
  output out_7,
  output out_8
);

  wire clock_1_out, not_1_out, not_2_out, not_3_out, not_4_out, not_5_out, not_6_out, or_1_out;

  Clock clock_1 (.out(clock_1_out));
  not not_1 (not_1_out, or_1_out);
  or or_1 (or_1_out, out_8, in_1);
  J_K_Flip_Flop j_k_ff_1 (
    .J(or_1_out), .clk(clock_1_out), .K(not_1_out), .Q(out_3), .reset(clear));  // open: Qn, preset, en
  J_K_Flip_Flop j_k_ff_2 (
    .J(out_3), .clk(clock_1_out), .K(not_2_out), .Q(out_4), .reset(clear));  // open: Qn, preset, en
  not not_2 (not_2_out, out_3);
  J_K_Flip_Flop j_k_ff_3 (
    .J(out_4), .clk(clock_1_out), .K(not_3_out), .Q(out_5), .reset(clear));  // open: Qn, preset, en
  not not_3 (not_3_out, out_4);
  not not_4 (not_4_out, out_5);
  J_K_Flip_Flop j_k_ff_4 (
    .J(out_5), .clk(clock_1_out), .K(not_4_out), .Q(out_6), .reset(clear));  // open: Qn, preset, en
  not not_5 (not_5_out, out_6);
  J_K_Flip_Flop j_k_ff_5 (
    .J(out_6), .clk(clock_1_out), .K(not_5_out), .Q(out_7), .reset(clear));  // open: Qn, preset, en
  J_K_Flip_Flop j_k_ff_6 (
    .J(out_7), .clk(clock_1_out), .K(not_6_out), .Q(out_8), .reset(clear));  // open: Qn, preset, en
  not not_6 (not_6_out, out_7);
endmodule
