// Logisim project Exercicio05.circ as structural Verilog: 1 circuit, main circuit main
module main (
  input  clear,
  input  in_2,
  input  in_3,
  input  in_4,
  input  in_5,
  input  in_6,
  input  in_7,
  input  in_8,
  output out_9,
  output out_10,
  output out_11,
  output out_12,
  output out_13,
  output out_14
);

  wire and_1_out, and_2_out, and_3_out, and_4_out, and_5_out, and_6_out, clock_1_out, not_1_out, not_2_out,
       not_3_out, not_4_out, not_5_out, not_6_out;

  Clock clock_1 (.out(clock_1_out));
  not not_1 (not_1_out, 1'b0);
  J_K_Flip_Flop j_k_ff_1 (
    .J(1'b0), .clk(clock_1_out), .K(not_1_out), .Q(out_9), .preset(and_1_out), .reset(clear));  // open: Qn, en
  and and_1 (and_1_out, in_2, in_3);
  J_K_Flip_Flop j_k_ff_2 (
    .J(out_9), .clk(clock_1_out), .K(not_2_out), .Q(out_10), .preset(and_2_out), .reset(clear));  // open: Qn, en
  not not_2 (not_2_out, out_9);
  and and_2 (and_2_out, in_2, in_4);
  J_K_Flip_Flop j_k_ff_3 (
    .J(out_10), .clk(clock_1_out), .K(not_3_out), .Q(out_11), .preset(and_3_out), .reset(clear));  // open: Qn, en
  not not_3 (not_3_out, out_10);
  and and_3 (and_3_out, in_2, in_5);
  not not_4 (not_4_out, out_11);
  and and_4 (and_4_out, in_2, in_6);
  J_K_Flip_Flop j_k_ff_4 (
    .J(out_11), .clk(clock_1_out), .K(not_4_out), .Q(out_12), .preset(and_4_out), .reset(clear));  // open: Qn, en
  not not_5 (not_5_out, out_12);
  J_K_Flip_Flop j_k_ff_5 (
    .J(out_12), .clk(clock_1_out), .K(not_5_out), .Q(out_13), .preset(and_5_out), .reset(clear));  // open: Qn, en
  and and_5 (and_5_out, in_2, in_7);
  J_K_Flip_Flop j_k_ff_6 (
    .J(out_13), .clk(clock_1_out), .K(not_6_out), .Q(out_14), .preset(and_6_out), .reset(clear));  // open: Qn, en
  not not_6 (not_6_out, out_13);
  and and_6 (and_6_out, in_2, in_8);
endmodule
