// Logisim project ExercicioA.circ as structural Verilog: 1 circuit, main circuit main
module main (
  input  in_1,
  input  in_2,
  input  in_3,
  input  in_4,
  output out_5
);

  wire and_1_out, and_2_out, and_3_out, and_4_out, and_5_out, and_6_out, and_7_out, and_8_out, and_9_out,
       and_10_out, and_11_out, and_12_out, and_13_out, and_14_out, and_15_out, and_16_out, not_1_out,
       not_2_out, not_3_out, not_4_out, or_1_out, or_2_out;

  not not_1 (not_1_out, in_2);
  not not_2 (not_2_out, in_1);
  not not_3 (not_3_out, in_3);
  not not_4 (not_4_out, in_4);
  and and_1 (and_1_out, not_4_out, not_3_out, not_1_out, not_2_out);
  and and_2 (and_2_out, in_4, not_3_out, not_1_out, not_2_out);
  and and_3 (and_3_out, not_4_out, in_3, not_1_out, not_2_out);
  and and_4 (and_4_out, in_4, in_3, not_1_out, not_2_out);
  and and_5 (and_5_out, not_4_out, not_3_out, in_2, not_2_out);
  and and_6 (and_6_out, in_4, not_3_out, in_2, not_2_out);
  and and_7 (and_7_out, not_4_out, in_3, in_2, not_2_out);
  and and_8 (and_8_out, in_4, in_3, in_2, not_2_out);
  and and_9 (and_9_out, not_4_out, not_3_out, not_1_out, in_1);
  and and_10 (and_10_out, in_4, in_3, in_2, in_1);
  and and_11 (and_11_out, in_4, not_3_out, not_1_out, in_1);
  and and_12 (and_12_out, not_4_out, in_3, not_1_out, in_1);
  and and_13 (and_13_out, in_4, in_3, not_1_out, in_1);
  and and_14 (and_14_out, not_4_out, not_3_out, in_2, in_1);
  and and_15 (and_15_out, in_4, not_3_out, in_2, in_1);
  and and_16 (and_16_out, not_4_out, in_3, in_2, in_1);
  or or_1 (or_1_out, and_1_out, and_2_out, and_3_out, and_4_out, and_5_out, and_6_out, and_7_out, and_8_out);
  or or_2 (or_2_out, and_9_out, and_10_out, and_11_out, and_12_out, and_13_out, and_14_out, and_15_out, and_16_out);
  or or_3 (out_5, or_1_out, or_2_out);
endmodule
