// Logisim project ExercicioB.circ as structural Verilog: 1 circuit, main circuit main
module main (
  input  in_1,
  input  in_2,
  input  in_3,
  input  in_4,
  output out_5
);

  wire and_1_out, and_2_out, not_1_out, not_2_out, not_3_out, not_4_out, or_1_out, or_2_out, or_3_out,
       or_4_out, or_5_out, or_6_out, or_7_out, or_8_out, or_9_out, or_10_out, or_11_out, or_12_out,
       or_13_out, or_14_out, or_15_out, or_16_out;

  not not_1 (not_1_out, in_2);
  not not_2 (not_2_out, in_1);
  not not_3 (not_3_out, in_3);
  not not_4 (not_4_out, in_4);
  or or_1 (or_1_out, not_4_out, not_3_out, not_1_out, not_2_out);
  or or_2 (or_2_out, in_4, not_3_out, not_1_out, not_2_out);
  or or_3 (or_3_out, not_4_out, in_3, not_1_out, not_2_out);
  or or_4 (or_4_out, in_4, in_3, not_1_out, not_2_out);
  or or_5 (or_5_out, not_4_out, not_3_out, in_2, not_2_out);
  or or_6 (or_6_out, in_4, not_3_out, in_2, not_2_out);
  or or_7 (or_7_out, not_4_out, in_3, in_2, not_2_out);
  or or_8 (or_8_out, in_4, in_3, in_2, not_2_out);
  or or_9 (or_9_out, not_4_out, not_3_out, not_1_out, in_1);
  or or_10 (or_10_out, in_4, in_3, in_2, in_1);
  or or_11 (or_11_out, in_4, not_3_out, not_1_out, in_1);
  or or_12 (or_12_out, not_4_out, in_3, not_1_out, in_1);
  or or_13 (or_13_out, in_4, in_3, not_1_out, in_1);
  or or_14 (or_14_out, not_4_out, not_3_out, in_2, in_1);
  or or_15 (or_15_out, in_4, not_3_out, in_2, in_1);
  or or_16 (or_16_out, not_4_out, in_3, in_2, in_1);
  and and_1 (and_1_out, or_1_out, or_2_out, or_3_out, or_4_out, or_5_out, or_6_out, or_7_out, or_8_out);
  and and_2 (and_2_out, or_9_out, or_10_out, or_11_out, or_12_out, or_13_out, or_14_out, or_15_out, or_16_out);
  and and_3 (out_5, and_1_out, and_2_out);
endmodule
