// Logisim project ExercicioE.circ as structural Verilog: 1 circuit, main circuit main
module main (
  input  in_1,
  input  in_2,
  input  in_3,
  output out_4
);

  wire nand_1_out, nand_2_out, nand_3_out, nand_4_out, nand_5_out, nand_6_out, nand_7_out, nand_8_out,
       nand_9_out, nand_10_out, nand_11_out, nand_12_out, nand_13_out, nand_14_out, nand_15_out, nand_16_out,
       not_1_out, not_2_out, not_3_out, not_4_out, not_5_out, not_6_out, not_7_out, not_8_out, not_9_out,
       not_10_out, not_11_out, not_12_out;

  not not_1 (not_1_out, in_3);
  not not_2 (not_2_out, in_2);
  not not_3 (not_3_out, in_3);
  not not_4 (not_4_out, in_2);
  not not_5 (not_5_out, in_1);
  not not_6 (not_6_out, in_3);
  not not_7 (not_7_out, in_1);
  not not_8 (not_8_out, in_2);
  not not_9 (not_9_out, in_1);
  not not_10 (not_10_out, in_3);
  not not_11 (not_11_out, in_2);
  not not_12 (not_12_out, in_1);
  nand nand_1 (nand_1_out, in_3, in_2, in_1);
  nand nand_2 (nand_2_out, nand_1_out, nand_1_out);
  nand nand_3 (nand_3_out, nand_4_out, nand_4_out);
  nand nand_4 (nand_4_out, not_1_out, in_2, in_1);
  nand nand_5 (nand_5_out, in_3, not_2_out, in_1);
  nand nand_6 (nand_6_out, nand_5_out, nand_5_out);
  nand nand_7 (nand_7_out, nand_8_out, nand_8_out);
  nand nand_8 (nand_8_out, not_3_out, not_4_out, in_1);
  nand nand_9 (nand_9_out, in_3, in_2, not_5_out);
  nand nand_10 (nand_10_out, nand_9_out, nand_9_out);
  nand nand_11 (nand_11_out, not_6_out, in_2, not_7_out);
  nand nand_12 (nand_12_out, nand_11_out, nand_11_out);
  nand nand_13 (nand_13_out, nand_14_out, nand_14_out);
  nand nand_14 (nand_14_out, in_3, not_8_out, not_9_out);
  nand nand_15 (nand_15_out, not_10_out, not_11_out, not_12_out);
  nand nand_16 (nand_16_out, nand_15_out, nand_15_out);
  nand nand_17 (out_4, nand_2_out, nand_3_out, nand_6_out, nand_7_out, nand_10_out, nand_12_out, nand_13_out, nand_16_out);
endmodule
