// Logisim project ExercicioF.circ as structural Verilog: 1 circuit, main circuit main
module main (
  input  in_1,
  input  in_2,
  input  in_3,
  output out_4
);

  wire nor_1_out, nor_2_out, nor_3_out, nor_4_out, nor_5_out, nor_6_out, nor_7_out, nor_8_out, nor_9_out,
       nor_10_out, nor_11_out, nor_12_out, nor_13_out, nor_14_out, nor_15_out, nor_16_out, not_1_out,
       not_2_out, not_3_out, not_4_out, not_5_out, not_6_out, not_7_out, not_8_out, not_9_out, not_10_out,
       not_11_out, not_12_out;

  not not_1 (not_1_out, in_3);
  not not_2 (not_2_out, in_2);
  not not_3 (not_3_out, in_3);
  not not_4 (not_4_out, in_2);
  not not_5 (not_5_out, in_1);
  not not_6 (not_6_out, in_3);
  not not_7 (not_7_out, in_1);
  not not_8 (not_8_out, in_2);
  not not_9 (not_9_out, in_1);
  not not_10 (not_10_out, in_3);
  not not_11 (not_11_out, in_2);
  not not_12 (not_12_out, in_1);
  nor nor_1 (nor_1_out, in_3, in_2, in_1);
  nor nor_2 (nor_2_out, nor_1_out, nor_1_out);
  nor nor_3 (nor_3_out, not_1_out, in_2, in_1);
  nor nor_4 (nor_4_out, nor_3_out, nor_3_out);
  nor nor_5 (nor_5_out, nor_6_out, nor_6_out);
  nor nor_6 (nor_6_out, in_3, not_2_out, in_1);
  nor nor_7 (nor_7_out, not_3_out, not_4_out, in_1);
  nor nor_8 (nor_8_out, nor_7_out, nor_7_out);
  nor nor_9 (nor_9_out, nor_10_out, nor_10_out);
  nor nor_10 (nor_10_out, in_3, in_2, not_5_out);
  nor nor_11 (nor_11_out, not_6_out, in_2, not_7_out);
  nor nor_12 (nor_12_out, nor_11_out, nor_11_out);
  nor nor_13 (nor_13_out, in_3, not_8_out, not_9_out);
  nor nor_14 (nor_14_out, nor_13_out, nor_13_out);
  nor nor_15 (nor_15_out, not_10_out, not_11_out, not_12_out);
  nor nor_16 (nor_16_out, nor_15_out, nor_15_out);
  nor nor_17 (out_4, nor_2_out, nor_4_out, nor_5_out, nor_8_out, nor_9_out, nor_12_out, nor_14_out, nor_16_out);
endmodule
