// Logisim project ExercicioA.circ as structural Verilog: 1 circuit, main circuit main
module main (
  input  in_1,
  input  in_2,
  input  in_3
);

  wire multiplexer_1_out, multiplexer_2_out, multiplexer_3_out, not_1_out, not_2_out, not_3_out;

  not not_1 (not_1_out, in_2);
  Multiplexer multiplexer_1 (.in0(not_1_out), .in1(in_2), .out(multiplexer_1_out), .sel(in_3));  // open: en
  not not_2 (not_2_out, in_2);
  Multiplexer multiplexer_2 (.in0(not_2_out), .in1(in_2), .out(multiplexer_2_out), .sel(not_3_out));  // open: en
  not not_3 (not_3_out, in_3);
  Multiplexer multiplexer_3 (
    .in0(multiplexer_1_out), .in1(multiplexer_2_out), .out(multiplexer_3_out), .sel(in_1));  // open: en
endmodule
