// Logisim project FlipFLopD.circ as structural Verilog: 1 circuit, main circuit main
module main (
  input  B,
  input  C,
  input  A
);

  wire and_1_out, clock_1_out, d_ff_1_q, not_1_out, not_2_out;

  Clock clock_1 (.out(clock_1_out));
  not not_1 (not_1_out, C);
  not not_2 (not_2_out, A);
  and and_1 (and_1_out, not_1_out, not_2_out);
  D_Flip_Flop d_ff_1 (.clk(clock_1_out), .D(and_1_out), .Q(d_ff_1_q));  // open: Qn, preset, en, reset
endmodule
