// Logisim project FlipFLopJaKa.circ as structural Verilog: 1 circuit, main circuit main
module main (
  input  B,
  input  C,
  input  A
);

  wire and_1_out, clock_1_out, not_1_out, not_2_out;

  Clock clock_1 (.out(clock_1_out));
  not not_1 (not_1_out, C);
  not not_2 (not_2_out, A);
  and and_1 (and_1_out, not_1_out, not_2_out);
  J_K_Flip_Flop j_k_ff_1 (.J(and_1_out), .clk(clock_1_out), .K(A));  // open: Q, Qn, preset, en, reset
endmodule
