// Logisim project FlipFLopSbRb.circ as structural Verilog: 1 circuit, main circuit main
module main (
  input  C,
  input  B,
  input  A
);

  wire and_1_out, and_2_out, and_3_out, clock_1_out, not_1_out, not_2_out, not_3_out, or_1_out, s_r_ff_1_q;

  Clock clock_1 (.out(clock_1_out));
  not not_1 (not_1_out, B);
  and and_1 (and_1_out, C, not_1_out);
  not not_2 (not_2_out, C);
  and and_2 (and_2_out, not_2_out, B, A);
  and and_3 (and_3_out, C, B, not_3_out);
  not not_3 (not_3_out, A);
  or or_1 (or_1_out, and_2_out, and_3_out);
  S_R_Flip_Flop s_r_ff_1 (
    .S(and_1_out), .clk(clock_1_out), .R(or_1_out), .Q(s_r_ff_1_q));  // open: Qn, preset, reset, en
endmodule
