// Logisim project FlipFLopTa.circ as structural Verilog: 1 circuit, main circuit main
module main (
  input  B,
  input  C,
  input  A
);

  wire and_1_out, clock_1_out, not_1_out, not_2_out, or_1_out;

  Clock clock_1 (.out(clock_1_out));
  not not_1 (not_1_out, C);
  not not_2 (not_2_out, A);
  and and_1 (and_1_out, not_1_out, not_2_out);
  or or_1 (or_1_out, A, and_1_out);
  T_Flip_Flop t_ff_1 (.clk(clock_1_out), .T(or_1_out));  // open: Q, Qn, preset, reset, en
endmodule
