// Logisim project FlipFLopTb.circ as structural Verilog: 1 circuit, main circuit main
module main (
  input  A,
  input  B,
  input  C
);

  wire and_1_out, and_2_out, and_3_out, clock_1_out, not_1_out, not_2_out, not_3_out, or_1_out, t_ff_1_q;

  Clock clock_1 (.out(clock_1_out));
  and and_1 (and_1_out, C, not_1_out);
  not not_1 (not_1_out, A);
  and and_2 (and_2_out, C, not_2_out, A);
  not not_2 (not_2_out, B);
  not not_3 (not_3_out, C);
  and and_3 (and_3_out, not_3_out, B, A);
  or or_1 (or_1_out, and_1_out, and_2_out, and_3_out);
  T_Flip_Flop t_ff_1 (.clk(clock_1_out), .T(or_1_out), .Q(t_ff_1_q));  // open: Qn, preset, reset, en
endmodule
