// Logisim project exercicio5A.circ as structural Verilog: 1 circuit, main circuit main
module main (
  input  C,
  input  A
);

  wire clock_1_out, d_ff_1_q, nand_1_out, nand_2_out, not_1_out, not_2_out;

  Clock clock_1 (.out(clock_1_out));
  not not_1 (not_1_out, C);
  not not_2 (not_2_out, A);
  nand nand_1 (nand_1_out, not_1_out, not_2_out);
  nand nand_2 (nand_2_out, nand_1_out, nand_1_out);
  D_Flip_Flop d_ff_1 (.clk(clock_1_out), .D(nand_2_out), .Q(d_ff_1_q));  // open: Qn, preset, en, reset
endmodule
