// Logisim project exercicio5B.circ as structural Verilog: 1 circuit, main circuit main
module main (
  input  C,
  input  B
);

  wire and_1_out, clock_1_out, nor_1_out, nor_2_out, nor_3_out, not_1_out, not_2_out, not_3_out, not_4_out,
       s_r_ff_1_q, s_r_ff_2_q;

  Clock clock_1 (.out(clock_1_out));
  not not_1 (not_1_out, B);
  not not_2 (not_2_out, B);
  and and_1 (and_1_out, C, not_1_out);
  nor nor_1 (nor_1_out, C, C);
  nor nor_2 (nor_2_out, not_2_out, not_2_out);
  not not_3 (not_3_out, and_1_out);
  nor nor_3 (nor_3_out, nor_1_out, nor_2_out);
  not not_4 (not_4_out, nor_3_out);
  S_R_Flip_Flop s_r_ff_1 (
    .S(and_1_out), .clk(clock_1_out), .R(not_3_out), .Q(s_r_ff_1_q));  // open: Qn, preset, reset, en
  S_R_Flip_Flop s_r_ff_2 (
    .S(nor_3_out), .clk(clock_1_out), .R(not_4_out), .Q(s_r_ff_2_q));  // open: Qn, preset, reset, en
endmodule
