// Logisim project exercicoExtra1.circ as structural Verilog: 1 circuit, main circuit main
module main (
  input  in_1,
  input  load
);

  wire clock_1_out, t_ff_1_q, t_ff_3_q;

  Clock clock_1 (.out(clock_1_out));
  T_Flip_Flop t_ff_1 (.clk(clock_1_out), .T(in_1), .Q(t_ff_1_q), .reset(load));  // open: Qn, preset, en
  T_Flip_Flop t_ff_2 (.clk(clock_1_out), .T(t_ff_3_q), .preset(load));  // open: Q, Qn, reset, en
  T_Flip_Flop t_ff_3 (.clk(clock_1_out), .T(t_ff_1_q), .Q(t_ff_3_q), .preset(load));  // open: Qn, reset, en
endmodule
