// Logisim project exercicoExtra2.circ as structural Verilog: 1 circuit, main circuit main
module main (
  input  in_1,
  input  clear,
  input  load,
  input  in_4
);

  wire and_1_out, and_2_out, and_3_out, clock_1_out, d_ff_1_q, d_ff_2_q, d_ff_3_q, or_1_out;

  Clock clock_1 (.out(clock_1_out));
  or or_1 (or_1_out, d_ff_3_q, in_1);
  and and_1 (and_1_out, load, 1'b1);
  D_Flip_Flop d_ff_1 (
    .clk(clock_1_out), .D(or_1_out), .Q(d_ff_1_q), .preset(and_1_out), .reset(clear));  // open: Qn, en
  D_Flip_Flop d_ff_2 (
    .clk(clock_1_out), .D(d_ff_1_q), .Q(d_ff_2_q), .preset(and_2_out), .reset(clear));  // open: Qn, en
  and and_2 (and_2_out, load, 1'b1);
  D_Flip_Flop d_ff_3 (
    .clk(clock_1_out), .D(d_ff_2_q), .Q(d_ff_3_q), .preset(and_3_out), .reset(clear));  // open: Qn, en
  and and_3 (and_3_out, load, in_4);
endmodule
