// Logisim project Exercício Prático 1.circ as structural Verilog: 4 circuits, main circuit main
module main (
  input  in_1,
  input  in_2,
  input  in_3,
  input  in_4,
  input  in_5,
  input  in_6,
  input  in_7,
  input  in_8,
  input  in_9,
  output vai_um,
  output overflow
);

  wire decodificador_1_e, decodificador_1_f, decodificador_1_g, decodificador_1_h, decodificador_1_i,
       decodificador_1_j, decodificador_1_k, decodificador_2_e, decodificador_2_f, decodificador_2_g,
       decodificador_2_h, decodificador_2_i, decodificador_2_j, decodificador_2_k, decodificador_3_e,
       decodificador_3_f, decodificador_3_g, decodificador_3_h, decodificador_3_i, decodificador_3_j,
       decodificador_3_k, somador_4_bits_1_out_10, somador_4_bits_1_out_11, somador_4_bits_1_out_12,
       somador_4_bits_1_out_13;

  somador_4_bits somador_4_bits_1 (
    .a0(in_1), .a1(in_3), .a2(in_4), .a3(in_5), .b0(in_6), .b1(in_7), .b2(in_8), .b3(in_9),
    .out_10(somador_4_bits_1_out_10), .out_11(somador_4_bits_1_out_11), .out_12(somador_4_bits_1_out_12),
    .out_13(somador_4_bits_1_out_13), .in_1(in_2), .overflow(overflow), .vai_um(vai_um));
  decodificador decodificador_1 (
    .A(in_5), .B(in_4), .C(in_3), .D(in_1), .e(decodificador_1_e), .f(decodificador_1_f),
    .g(decodificador_1_g), .h(decodificador_1_h), .i(decodificador_1_i), .j(decodificador_1_j),
    .k(decodificador_1_k));
  decodificador decodificador_2 (
    .A(in_9), .B(in_8), .C(in_7), .D(in_6), .e(decodificador_2_e), .f(decodificador_2_f),
    .g(decodificador_2_g), .h(decodificador_2_h), .i(decodificador_2_i), .j(decodificador_2_j),
    .k(decodificador_2_k));
  _7_Segment_Display u_7_segment_display_1 (
    .g(decodificador_1_k), .f(decodificador_1_j), .a(decodificador_1_e), .b(decodificador_1_f),
    .e(decodificador_1_i), .d(decodificador_1_h), .c(decodificador_1_g));  // open: dp
  decodificador decodificador_3 (
    .A(somador_4_bits_1_out_13), .B(somador_4_bits_1_out_12), .C(somador_4_bits_1_out_11),
    .D(somador_4_bits_1_out_10), .e(decodificador_3_e), .f(decodificador_3_f), .g(decodificador_3_g),
    .h(decodificador_3_h), .i(decodificador_3_i), .j(decodificador_3_j), .k(decodificador_3_k));
  _7_Segment_Display u_7_segment_display_2 (
    .g(decodificador_2_k), .f(decodificador_2_j), .a(decodificador_2_e), .b(decodificador_2_f),
    .e(decodificador_2_i), .d(decodificador_2_h), .c(decodificador_2_g));  // open: dp
  _7_Segment_Display u_7_segment_display_3 (
    .g(decodificador_3_k), .f(decodificador_3_j), .a(decodificador_3_e), .b(decodificador_3_f),
    .e(decodificador_3_i), .d(decodificador_3_h), .c(decodificador_3_g));  // open: dp
endmodule

module somador (
  input  vem_um,
  input  A,
  input  B,
  output saida,
  output vai_um
);

  wire and_1_out, and_2_out, xor_1_out;

  xor xor_1 (xor_1_out, A, B);
  and and_1 (and_1_out, A, B);
  xor xor_2 (saida, vem_um, xor_1_out);
  and and_2 (and_2_out, xor_1_out, vem_um);
  or or_1 (vai_um, and_2_out, and_1_out);
endmodule

module somador_4_bits (
  input  in_1,
  input  a0,
  input  a1,
  input  a2,
  input  a3,
  input  b0,
  input  b1,
  input  b2,
  input  b3,
  output out_10,
  output out_11,
  output out_12,
  output out_13,
  output overflow,
  output vai_um
);

  wire somador_1_vai_um, somador_2_vai_um, somador_3_vai_um;

  somador somador_1 (.A(a0), .B(b0), .vem_um(in_1), .vai_um(somador_1_vai_um), .saida(out_10));
  somador somador_2 (.A(a1), .B(b1), .vem_um(somador_1_vai_um), .vai_um(somador_2_vai_um), .saida(out_11));
  somador somador_3 (.A(a2), .B(b2), .vem_um(somador_2_vai_um), .vai_um(somador_3_vai_um), .saida(out_12));
  somador somador_4 (.A(a3), .B(b3), .vem_um(somador_3_vai_um), .vai_um(vai_um), .saida(out_13));
  xor xor_1 (overflow, somador_3_vai_um, vai_um);
endmodule

module decodificador (
  input  A,
  input  B,
  input  C,
  input  D,
  output e,
  output f,
  output g,
  output h,
  output i,
  output j,
  output k
);

  wire and_1_out, and_2_out, and_3_out, and_4_out, and_5_out, and_6_out, and_7_out, and_8_out, and_9_out,
       and_10_out, and_11_out, and_12_out, and_13_out, and_14_out, and_15_out, and_16_out, and_17_out,
       and_18_out, and_19_out, and_20_out, and_21_out, and_22_out, and_23_out, and_24_out, and_25_out,
       and_26_out, and_27_out, and_28_out, and_29_out, and_30_out, and_31_out, and_32_out, not_1_out,
       not_2_out, not_3_out, not_4_out, not_5_out, not_6_out, not_7_out, not_8_out, not_9_out, not_10_out,
       not_11_out, not_12_out, not_13_out, not_14_out, not_15_out, not_16_out, not_17_out, not_18_out,
       not_19_out, not_20_out, not_21_out, not_22_out, not_23_out, not_24_out, not_25_out, not_26_out,
       not_27_out, not_28_out, not_29_out, not_30_out, not_31_out, not_32_out, not_33_out, not_34_out,
       not_35_out, not_36_out, not_37_out, not_38_out, not_39_out, not_40_out, not_41_out, not_42_out;

  not not_1 (not_1_out, B);
  and and_1 (and_1_out, not_1_out, not_2_out);
  not not_2 (not_2_out, D);
  not not_3 (not_3_out, A);
  and and_2 (and_2_out, not_3_out, C);
  not not_4 (not_4_out, A);
  and and_3 (and_3_out, not_4_out, B, D);
  and and_4 (and_4_out, B, C);
  not not_5 (not_5_out, B);
  and and_5 (and_5_out, A, not_5_out, not_6_out);
  not not_6 (not_6_out, C);
  not not_7 (not_7_out, A);
  and and_6 (and_6_out, not_7_out, not_8_out);
  not not_8 (not_8_out, B);
  not not_9 (not_9_out, A);
  and and_7 (and_7_out, not_9_out, not_10_out, not_11_out);
  not not_10 (not_10_out, C);
  not not_11 (not_11_out, D);
  not not_12 (not_12_out, B);
  and and_8 (and_8_out, not_12_out, not_13_out);
  not not_13 (not_13_out, D);
  not not_14 (not_14_out, A);
  and and_9 (and_9_out, not_14_out, C, D);
  and and_10 (and_10_out, A, not_15_out, D);
  not not_15 (not_15_out, C);
  not not_16 (not_16_out, A);
  and and_11 (and_11_out, not_16_out, not_17_out);
  not not_17 (not_17_out, C);
  not not_18 (not_18_out, A);
  and and_12 (and_12_out, not_18_out, D);
  not not_19 (not_19_out, C);
  and and_13 (and_13_out, not_19_out, D);
  not not_20 (not_20_out, A);
  and and_14 (and_14_out, not_20_out, B);
  and and_15 (and_15_out, A, not_21_out);
  not not_21 (not_21_out, B);
  not not_22 (not_22_out, A);
  not not_23 (not_23_out, B);
  and and_16 (and_16_out, not_22_out, not_23_out, not_24_out);
  not not_24 (not_24_out, D);
  not not_25 (not_25_out, B);
  and and_17 (and_17_out, not_25_out, C, D);
  and and_18 (and_18_out, B, not_26_out, D);
  not not_26 (not_26_out, C);
  and and_19 (and_19_out, B, C, not_27_out);
  not not_27 (not_27_out, D);
  and and_20 (and_20_out, A, not_28_out);
  not not_28 (not_28_out, C);
  not not_29 (not_29_out, B);
  and and_21 (and_21_out, not_29_out, not_30_out);
  not not_30 (not_30_out, D);
  and and_22 (and_22_out, C, not_31_out);
  not not_31 (not_31_out, D);
  and and_23 (and_23_out, A, C);
  and and_24 (and_24_out, A, B);
  not not_32 (not_32_out, A);
  not not_33 (not_33_out, C);
  and and_25 (and_25_out, not_32_out, not_33_out, not_34_out);
  not not_34 (not_34_out, D);
  not not_35 (not_35_out, A);
  and and_26 (and_26_out, not_35_out, B, not_36_out);
  not not_36 (not_36_out, C);
  not not_37 (not_37_out, A);
  and and_27 (and_27_out, not_37_out, B, not_38_out);
  not not_38 (not_38_out, D);
  and and_28 (and_28_out, A, not_39_out);
  not not_39 (not_39_out, B);
  and and_29 (and_29_out, A, C);
  not not_40 (not_40_out, B);
  and and_30 (and_30_out, not_40_out, C);
  and and_31 (and_31_out, B, not_41_out);
  not not_41 (not_41_out, C);
  and and_32 (and_32_out, B, not_42_out);
  not not_42 (not_42_out, D);
  or or_1 (e, and_1_out, and_2_out, and_3_out, and_4_out, and_5_out);
  or or_2 (f, and_6_out, and_7_out, and_8_out, and_9_out, and_10_out);
  or or_3 (g, and_11_out, and_12_out, and_13_out, and_14_out, and_15_out);
  or or_4 (h, and_16_out, and_17_out, and_18_out, and_19_out, and_20_out);
  or or_5 (i, and_21_out, and_22_out, and_23_out, and_24_out);
  or or_6 (j, and_25_out, and_26_out, and_27_out, and_28_out, and_29_out);
  or or_7 (k, and_30_out, and_31_out, and_32_out, A);
endmodule
