// Logisim project ULA completa.circ as structural Verilog: 7 circuits, main circuit main
module main (
  input  in_1,
  input  in_2,
  input  in_3,
  input  in_4,
  input  in_5,
  input  in_6,
  input  in_7,
  input  in_8,
  input  binvert,
  input  in_10,
  input  in_11,
  input  x,
  input  y,
  input  w,
  output out_15,
  output out_16,
  output out_17,
  output out_18
);

  wire clock_1_out, ula_completa_1_co, ula_completa_1_s0, ula_completa_1_s1, ula_completa_1_s2,
       ula_completa_1_s3;

  ULA_completa ula_completa_1 (
    .in_1(in_1), .in_2(in_2), .in_3(in_3), .in_4(in_4), .in_5(in_5), .in_6(in_6), .in_7(in_7), .in_8(in_8),
    .binvert(binvert), .in_10(in_10), .in_11(in_11), .co(ula_completa_1_co), .s0(ula_completa_1_s0),
    .s1(ula_completa_1_s1), .s2(ula_completa_1_s2), .s3(ula_completa_1_s3));
  register register_1 (
    .in_1(ula_completa_1_s3), .in_2(ula_completa_1_s2), .in_3(ula_completa_1_s1), .in_4(ula_completa_1_s0),
    .out_9(out_15), .out_10(out_16), .out_11(out_17), .out_12(out_18), .x(x), .y(y), .w(w),
    .clock(clock_1_out));
  Clock clock_1 (.out(clock_1_out));
endmodule

module Somatorio (
  input  c1,
  input  a,
  input  b,
  output s0,
  output c0
);

  wire and_1_out, and_2_out, xor_1_out;

  and and_1 (and_1_out, b, a);
  or or_1 (c0, and_1_out, and_2_out);
  xor xor_1 (xor_1_out, a, b);
  and and_2 (and_2_out, xor_1_out, c1);
  xor xor_2 (s0, c1, xor_1_out);
endmodule

module ULA (
  input  binvert,
  input  cin,
  input  op1,
  input  op0,
  input  a,
  input  b,
  output S0,
  output co
);

  wire and_1_out, and_2_out, and_3_out, not_1_out, not_2_out, not_3_out, or_1_out, or_2_out, somatorio_1_s0;

  not not_1 (not_1_out, binvert);
  not not_2 (not_2_out, b);
  and and_1 (and_1_out, b, not_1_out);
  or or_1 (or_1_out, and_1_out, and_2_out);
  and and_2 (and_2_out, not_2_out, binvert);
  and and_3 (and_3_out, a, b);
  or or_2 (or_2_out, a, b);
  not not_3 (not_3_out, a);
  Somatorio somatorio_1 (.a(a), .s0(somatorio_1_s0), .c1(cin), .c0(co), .b(or_1_out));
  mux mux_1 (
    .in_3(and_3_out), .in_4(or_2_out), .in_5(not_3_out), .in_6(somatorio_1_s0), .in_1(op1), .in_2(op0),
    .out_7(S0));
endmodule

module mux (
  input  in_1,
  input  in_2,
  input  in_3,
  input  in_4,
  input  in_5,
  input  in_6,
  output out_7
);

  wire and_1_out, and_2_out, and_3_out, and_4_out, not_1_out, not_2_out, not_3_out, not_4_out;

  and and_1 (and_1_out, in_3, not_1_out, not_2_out);
  not not_1 (not_1_out, in_2);
  not not_2 (not_2_out, in_1);
  and and_2 (and_2_out, in_4, in_2, not_3_out);
  not not_3 (not_3_out, in_1);
  not not_4 (not_4_out, in_2);
  and and_3 (and_3_out, in_5, not_4_out, in_1);
  and and_4 (and_4_out, in_6, in_2, in_1);
  or or_1 (out_7, and_1_out, and_2_out, and_3_out, and_4_out);
endmodule

module register (
  input  in_1,
  input  in_2,
  input  in_3,
  input  in_4,
  input  x,
  input  y,
  input  w,
  input  clock,
  output out_9,
  output out_10,
  output out_11,
  output out_12
);

  wire and_1_out, register_mux_1_out_6, register_mux_2_out_6, register_mux_3_out_6, register_mux_4_out_6;

  register_mux register_mux_1 (.in_1(in_1), .in_2(1'b0), .in_3(out_10), .y(x), .x(y), .out_6(register_mux_1_out_6));
  D_Flip_Flop d_ff_1 (.clk(and_1_out), .D(register_mux_1_out_6), .Q(out_9));  // open: Qn, preset, reset
  register_mux register_mux_2 (.in_1(in_2), .in_2(out_9), .in_3(out_11), .y(x), .x(y), .out_6(register_mux_2_out_6));
  register_mux register_mux_3 (.in_1(in_3), .in_2(out_10), .in_3(out_12), .y(x), .x(y), .out_6(register_mux_3_out_6));
  D_Flip_Flop d_ff_2 (.clk(and_1_out), .D(register_mux_2_out_6), .Q(out_10));  // open: Qn, preset, reset
  D_Flip_Flop d_ff_3 (.clk(and_1_out), .D(register_mux_3_out_6), .Q(out_11));  // open: Qn, preset, reset
  register_mux register_mux_4 (.in_1(in_4), .in_2(out_11), .in_3(1'b0), .y(x), .x(y), .out_6(register_mux_4_out_6));
  D_Flip_Flop d_ff_4 (.clk(and_1_out), .D(register_mux_4_out_6), .Q(out_12));  // open: Qn, preset, reset
  and and_1 (and_1_out, w, clock);
endmodule

module register_mux (
  input  in_1,
  input  in_2,
  input  in_3,
  input  y,
  input  x,
  output out_6
);

  wire and_1_out, and_2_out, and_3_out, not_1_out, not_2_out, not_3_out, not_4_out;

  not not_1 (not_1_out, y);
  and and_1 (and_1_out, in_1, not_1_out, not_2_out);
  not not_2 (not_2_out, x);
  and and_2 (and_2_out, in_2, not_3_out, x);
  not not_3 (not_3_out, y);
  and and_3 (and_3_out, in_3, y, not_4_out);
  not not_4 (not_4_out, x);
  or or_1 (out_6, and_1_out, and_2_out, and_3_out);
endmodule

module ULA_completa (
  input  in_1,
  input  in_2,
  input  in_3,
  input  in_4,
  input  in_5,
  input  in_6,
  input  in_7,
  input  in_8,
  input  binvert,
  input  in_10,
  input  in_11,
  output s0,
  output s1,
  output s2,
  output s3,
  output co
);

  wire ula_1_co, ula_2_co, ula_3_co;

  ULA ula_1 (.a(in_4), .b(in_8), .binvert(binvert), .cin(binvert), .op1(in_10), .op0(in_11), .co(ula_1_co), .S0(s0));
  ULA ula_2 (.a(in_3), .b(in_7), .binvert(binvert), .cin(ula_1_co), .op1(in_10), .op0(in_11), .co(ula_2_co), .S0(s1));
  ULA ula_3 (.a(in_2), .b(in_6), .binvert(binvert), .cin(ula_2_co), .op1(in_10), .op0(in_11), .co(ula_3_co), .S0(s2));
  ULA ula_4 (.a(in_1), .b(in_5), .binvert(binvert), .cin(ula_3_co), .op1(in_10), .op0(in_11), .co(co), .S0(s3));
endmodule
